// Logisim project BF Computer.circ as structural Verilog: 5 circuits, main circuit main
module main (
  input  in_1,
  input  in_2
);

  wire button_1_out, button_2_out, clock_1_out, decoder_1_out0, decoder_1_out1, decoder_1_out3,
       logic_ram_1_p1, logic_ram_1_p2, logic_ram_1_p3, logic_ram_1_p5, logic_ram_1_p6, logic_ram_1_p7,
       logic_ram_1_p8, n74191_2_ripple_clock, n74191_3_ripple_clock, n74191_4_ripple_clock,
       n74191_6_ripple_clock, n74191_8_ripple_clock, n74191_9_ripple_clock, n74191_10_ripple_clock,
       n74374_2_p2, n74374_2_p3, n74374_2_p4, n74374_2_p5, n74374_2_p6, n74374_2_p7, n74374_2_p8,
       n74374_2_p9, nor_1_out, nor_2_out, or_1_out, undriven_2;
  wire [2:0] undriven;
  wire [3:0] multiplexer_1_out, n74191_9_qa;
  wire [7:0] buffer_2_out, n74374_2_p1, ram_1_data, rom_1_data;
  wire [15:0] n74191_4_qa, n74191_10_qa;

  nor nor_1 (nor_1_out, in_1, logic_ram_1_p5);
  _74191 u_74191_1 (
    .Data_B(1'b0), .QB(n74191_4_qa[13]), .QA(n74191_4_qa[12]), .Enable_G(nor_1_out), .Down_Up(in_1),
    .QC(n74191_4_qa[14]), .QD(n74191_4_qa[15]), .Data_A(1'b0), .Clock(n74191_2_ripple_clock), .Load(in_2),
    .Data_C(1'b0), .Data_D(1'b0));  // open: Gnd, Vcc, Ripple_Clock, Max___Min
  _74191 u_74191_2 (
    .Data_B(1'b0), .QB(n74191_4_qa[9]), .QA(n74191_4_qa[8]), .Enable_G(nor_1_out), .Down_Up(in_1),
    .QC(n74191_4_qa[10]), .QD(n74191_4_qa[11]), .Data_A(1'b0), .Clock(n74191_3_ripple_clock),
    .Ripple_Clock(n74191_2_ripple_clock), .Load(in_2), .Data_C(1'b0), .Data_D(1'b0));  // open: Gnd, Vcc, Max___Min
  _74191 u_74191_3 (
    .Data_B(1'b0), .QB(n74191_4_qa[5]), .QA(n74191_4_qa[4]), .Enable_G(nor_1_out), .Down_Up(in_1),
    .QC(n74191_4_qa[6]), .QD(n74191_4_qa[7]), .Data_A(1'b0), .Clock(n74191_4_ripple_clock),
    .Ripple_Clock(n74191_3_ripple_clock), .Load(in_2), .Data_C(1'b0), .Data_D(1'b0));  // open: Gnd, Vcc, Max___Min
  _74191 u_74191_4 (
    .Data_B(1'b0), .QB(n74191_4_qa[1]), .QA(n74191_4_qa[0]), .Enable_G(nor_1_out), .Down_Up(in_1),
    .QC(n74191_4_qa[2]), .QD(n74191_4_qa[3]), .Data_A(1'b0), .Clock(clock_1_out),
    .Ripple_Clock(n74191_4_ripple_clock), .Load(in_2), .Data_C(1'b0), .Data_D(1'b0));  // open: Gnd, Vcc, Max___Min
  Clock clock_1 (.out(clock_1_out));
  // LOGIC_RAM logic_ram_1: pin names not known; wires that end beside it: logic_ram_1_p1, logic_ram_1_p2, logic_ram_1_p3, in_1, logic_ram_1_p5, logic_ram_1_p6, logic_ram_1_p7, logic_ram_1_p8
  Button button_1 (.out(button_1_out));
  _74191 u_74191_5 (
    .Enable_G(1'b0), .Down_Up(button_1_out), .QD(logic_ram_1_p3), .Clock(n74191_6_ripple_clock),
    .Max___Min(logic_ram_1_p1), .Load(1'b0));  // open: Data_B, QB, QA, QC, Gnd, Vcc, Data_A, Ripple_Clock, Data_C, Data_D
  or or_1 (or_1_out, button_1_out, logic_ram_1_p8);
  Multiplexer #(.width(4), .enable("false")) multiplexer_1 (
    .in0(rom_1_data[3:0]), .in1(rom_1_data[7:4]), .out(multiplexer_1_out), .sel(n74191_4_qa[15]));
  ROM #(.addrWidth(15)) rom_1 (.addr(n74191_4_qa[14:0]), .data(rom_1_data));  // open: sel
  _74191 u_74191_6 (
    .Enable_G(1'b0), .Down_Up(button_1_out), .Clock(or_1_out), .Ripple_Clock(n74191_6_ripple_clock),
    .Max___Min(logic_ram_1_p2), .Load(1'b0));  // open: Data_B, QB, QA, QC, QD, Gnd, Vcc, Data_A, Data_C, Data_D
  // _74374 74374_1: pin names not known; wires that end beside it: logic_ram_1_p6, button_1_out, multiplexer_1_out[0], multiplexer_1_out[1], multiplexer_1_out[2], multiplexer_1_out[3], 1'b0, logic_ram_1_p7
  Decoder #(.select(3), .enable("false")) decoder_1 (
    .out0(decoder_1_out0), .out1(decoder_1_out1), .out3(decoder_1_out3), .sel(undriven));  // open: out2, out4, out5, out6, out7
  Button button_2 (.out(button_2_out));
  _74191 u_74191_7 (
    .Data_B(1'b0), .QB(n74191_10_qa[13]), .QA(n74191_10_qa[12]), .Enable_G(nor_2_out),
    .Down_Up(button_2_out), .QC(n74191_10_qa[14]), .QD(n74191_10_qa[15]), .Data_A(1'b0),
    .Clock(n74191_8_ripple_clock), .Load(undriven_2), .Data_C(1'b0), .Data_D(1'b0));  // open: Gnd, Vcc, Ripple_Clock, Max___Min
  _74191 u_74191_8 (
    .Data_B(1'b0), .QB(n74191_10_qa[9]), .QA(n74191_10_qa[8]), .Enable_G(nor_2_out), .Down_Up(button_2_out),
    .QC(n74191_10_qa[10]), .QD(n74191_10_qa[11]), .Data_A(1'b0), .Clock(n74191_9_ripple_clock),
    .Ripple_Clock(n74191_8_ripple_clock), .Load(undriven_2), .Data_C(1'b0), .Data_D(1'b0));  // open: Gnd, Vcc, Max___Min
  _74191 u_74191_9 (
    .Data_B(1'b0), .QB(n74191_9_qa[1]), .QA(n74191_9_qa[0]), .Enable_G(nor_2_out), .Down_Up(button_2_out),
    .QC(n74191_9_qa[2]), .QD(n74191_9_qa[3]), .Data_A(1'b0), .Clock(n74191_10_ripple_clock),
    .Ripple_Clock(n74191_9_ripple_clock), .Load(undriven_2), .Data_C(1'b0), .Data_D(1'b0));  // open: Gnd, Vcc, Max___Min
  _74191 u_74191_10 (
    .Data_B(1'b0), .QB(n74191_10_qa[1]), .QA(n74191_10_qa[0]), .Enable_G(nor_2_out), .Down_Up(button_2_out),
    .QC(n74191_10_qa[2]), .QD(n74191_10_qa[3]), .Data_A(1'b0), .Clock(nor_2_out),
    .Ripple_Clock(n74191_10_ripple_clock), .Load(undriven_2), .Data_C(1'b0), .Data_D(1'b0));  // open: Gnd, Vcc, Max___Min
  nor nor_2 (nor_2_out, button_2_out, decoder_1_out3);
  RAM #(.addrWidth(15), .bus("asynch")) ram_1 (
    .addr({n74191_10_qa[14:8], n74191_9_qa, n74191_10_qa[3:0]}), .data(ram_1_data));  // open: sel, ld, clr
  assign ram_1_data = n74374_2_p1;  // Buffer buffer_1, 8 bits wide
  assign buffer_2_out = ram_1_data;  // Buffer buffer_2, 8 bits wide
  // _74374 74374_2: pin names not known; wires that end beside it: n74374_2_p1, n74374_2_p2, n74374_2_p3, n74374_2_p4, n74374_2_p5, n74374_2_p6, n74374_2_p7, n74374_2_p8, n74374_2_p9
  _1_ROM u_1_rom_1 (
    .in_1(decoder_1_out0), .in_2(decoder_1_out1), .in_3(n74374_2_p2), .in_4(n74374_2_p3), .in_5(n74374_2_p4),
    .in_6(n74374_2_p5), .in_7(n74374_2_p6), .in_8(n74374_2_p7), .in_9(n74374_2_p8), .in_10(n74374_2_p9));  // open: out_11, out_12, out_13, out_14, out_15, out_16, out_17, out_18

  // Notes on the sheet:
  //   16 Bit Ripple Counter Array
  //   +/-
  //   +/-
  //   Problems with rising/ falling counters
  //   32k x 8 ROM (64k x 4)
  //   contents of rom_1 (hex, n*v repeats v):
  //   14615*0 4
  //   Need Asynchronous Counters
  //   +/-
  //   +/-
endmodule

// 2k x 8 ROM
module LOGIC_RAM (
  input  Max__Min_A,
  input  Max__MinB,
  input  Last_Bit,
  input  Instruction_0,
  input  Instruction_1,
  input  Instruction_2,
  input  Tape,
  input  in_8,
  output out_9,
  output out_10,
  output out_11,
  output Instruction_plus,
  output Instruction_minus,
  output Count____0,
  output Loop_plus,
  output Loop_minus
);


  assign Count____0 = 1'b0;
  assign Instruction_minus = 1'b0;
  assign Instruction_plus = 1'b0;
  assign Loop_minus = 1'b0;
  assign Loop_plus = 1'b0;
  assign out_9 = 1'b0;
  assign out_10 = 1'b0;
  assign out_11 = 1'b0;
endmodule

module _74191 (
  input  Data_B,
  input  Vcc,
  input  Data_A,
  input  Clock,
  input  Enable_G,
  input  Down_Up,
  input  Load,
  input  Data_C,
  input  Gnd,
  input  Data_D,
  output QB,
  output QA,
  output Ripple_Clock,
  output Max___Min,
  output QC,
  output QD
);

  wire controlled_buffer_1_out, counter_controller_1_a, counter_controller_1_b, not_1_out, not_2_out,
       or_1_out;

  not not_1 (not_1_out, Down_Up);
  not not_2 (not_2_out, Enable_G);
  Counter #(.width(4), .max('hf)) counter_1 (
    .load(counter_controller_1_a), .D({Data_D, Data_C, Data_B, Data_A}), .count(counter_controller_1_b),
    .Q({QD, QC, QB, QA}), .carry(Max___Min), .clk(or_1_out));  // open: clr
  or or_1 (or_1_out, Load, controlled_buffer_1_out);
  Counter_Controller counter_controller_1 (
    .Plus(Down_Up), .Minus(not_1_out), .Load(Load), .A(counter_controller_1_a), .B(counter_controller_1_b));
  assign controlled_buffer_1_out = not_2_out ? Clock : 1'bz;  // Controlled_Buffer controlled_buffer_1
  Pull_Resistor pull_resistor_1 (.node(controlled_buffer_1_out));
  and and_1 (Ripple_Clock, controlled_buffer_1_out, Max___Min);
endmodule

module Counter_Controller (
  input  Plus,
  input  Minus,
  input  Load,
  output A,
  output B
);

  wire and_1_out, and_2_out, and_3_out, not_1_out, not_2_out, not_3_out, not_4_out, not_5_out;

  not not_1 (not_1_out, Plus);
  not not_2 (not_2_out, Plus);
  not not_3 (not_3_out, Load);
  not not_4 (not_4_out, Minus);
  not not_5 (not_5_out, Load);
  and and_1 (and_1_out, not_1_out, Minus);
  and and_2 (and_2_out, not_2_out, Minus, not_3_out);
  and and_3 (and_3_out, Plus, not_4_out, not_5_out);
  or or_1 (A, Load, and_1_out);
  or or_2 (B, and_2_out, and_3_out);
endmodule

// 2k x 8 ROM
module _1_ROM (
  input  in_1,
  input  in_2,
  input  in_3,
  input  in_4,
  input  in_5,
  input  in_6,
  input  in_7,
  input  in_8,
  input  in_9,
  input  in_10,
  output out_11,
  output out_12,
  output out_13,
  output out_14,
  output out_15,
  output out_16,
  output out_17,
  output out_18
);

  wire [7:0] adder_1_out, subtractor_1_out;

  Subtractor subtractor_1 (
    .a({in_10, in_9, in_8, in_7, in_6, in_5, in_4, in_3}), .b(8'h1), .out(subtractor_1_out));  // open: bin, bout
  Adder adder_1 (
    .a(8'h1), .b({in_10, in_9, in_8, in_7, in_6, in_5, in_4, in_3}), .out(adder_1_out));  // open: cin, cout
  Multiplexer #(.select(2), .width(8)) multiplexer_1 (
    .in0({in_10, in_9, in_8, in_7, in_6, in_5, in_4, in_3}), .in1(adder_1_out), .in2(subtractor_1_out),
    .in3({in_10, in_9, in_8, in_7, in_6, in_5, in_4, in_3}),
    .out({out_18, out_17, out_16, out_15, out_14, out_13, out_12, out_11}), .sel({in_2, in_1}));  // open: en
endmodule
