// Logisim project BrainfuckHardware.circ as structural Verilog: 3 circuits, main circuit main
// ADD/SUB1
module main (
  input  in_1,
  input  in_2,
  input  in_3,
  input  in_4,
  input  in_5
);

  wire and_1_out, and_2_out, and_3_out, and_5_out, and_6_out, and_7_out, Clear_2_out, Clear_out, clock_1_out,
       controlled_buffer_1_out, not_1_out, or_1_out, or_2_out, undriven, undriven_2;
  wire [2:0] ram_1_data;
  wire [6:0] keyboard_1_data;
  wire [7:0] ADD_SUB1_out_3, counter_1_q, counter_2_q, multiplexer_1_out, ram_2_data, register_1_q,
       stack_memory_1_out_5;

  Counter counter_1 (
    .load(in_1), .D(stack_memory_1_out_5), .count(in_2), .Q(counter_1_q), .clk(controlled_buffer_1_out));  // open: carry, clr
  assign controlled_buffer_1_out = in_4 ? clock_1_out : 1'bz;  // Controlled_Buffer controlled_buffer_1
  Clock clock_1 (.out(clock_1_out));
  Stack_Memory stack_memory_1 (
    .Data_In(counter_1_q), .out_5(stack_memory_1_out_5), .Write(and_2_out), .Read(undriven_2), .in_4(undriven));
  and and_1 (and_1_out, not_1_out, controlled_buffer_1_out, ram_1_data[1]);
  RAM #(.dataWidth(3), .bus("separate")) ram_1 (
    .addr(counter_1_q), .data(ram_1_data), .str(in_3), .clk(controlled_buffer_1_out));  // open: din, sel, ld, clr
  and and_2 (and_2_out, ram_1_data[2], ~ram_1_data[0], ~ram_1_data[1], or_1_out);  // AND_Gate
  Counter counter_2 (.load(ram_1_data[0]), .count(in_5), .Q(counter_2_q), .clk(and_1_out));  // open: D, carry, clr
  or or_1 (or_1_out, ram_2_data[4], ram_2_data[7], ram_2_data[6], ram_2_data[5], ram_2_data[3], ram_2_data[2], ram_2_data[1], ram_2_data[0]);
  or or_2 (or_2_out, and_3_out, and_5_out);
  and and_3 (and_3_out, not_1_out, controlled_buffer_1_out, ~ram_1_data[1]);  // AND_Gate
  // AND_Gate and_4 has open pins: in0=ram_1_data[2], in1=ram_1_data[0], in2=ram_1_data[1], out=open
  Register #(.trigger("high")) register_1 (.D(ram_2_data), .Q(register_1_q), .clk(or_2_out));  // open: en, clr
  RAM #(.bus("separate")) ram_2 (
    .addr(counter_2_q), .din(multiplexer_1_out), .data(ram_2_data), .clk(or_2_out));  // open: str, sel, ld, clr
  and and_5 (and_5_out, controlled_buffer_1_out, and_7_out);
  ADD_SUB_1 ADD_SUB1 (.in_1(ram_1_data[0]), .in_2(register_1_q), .out_3(ADD_SUB1_out_3));
  Multiplexer #(.width(8)) multiplexer_1 (
    .in0(ADD_SUB1_out_3), .in1({1'b0, keyboard_1_data}), .out(multiplexer_1_out), .sel(and_7_out));  // open: en
  not not_1 (not_1_out, ram_1_data[2]);
  and and_6 (and_6_out, ram_1_data[0], ram_1_data[1], ram_1_data[2]);
  TTY #(.rows(1)) tty_1 (.data(ram_2_data[6:0]), .clk(controlled_buffer_1_out), .we(and_6_out), .clr(Clear_out));
  Keyboard keyboard_1 (
    .clk(controlled_buffer_1_out), .re(and_7_out), .clr(Clear_2_out), .data(keyboard_1_data));  // open: avail
  and and_7 (and_7_out, ~ram_1_data[0], ram_1_data[1], ram_1_data[2]);  // AND_Gate
  Button Clear (.out(Clear_out));
  Button Clear_2 (.out(Clear_2_out));

  // Notes on the sheet:
  //   000 | "+"
  //   001 | "-"
  //   010 | ">"
  //   011 | "<"
  //   100 | "["
  //   101 | "]"
  //   Code | Command
  //   "["
  //   +, -, >, <
  //   TAPE HEAD
  //   TAPE
  //   ADDER or Else | TAPE or PC Enable| ADD or SUB
  //   Problem: when switching addresses, tape becomes the old tape address +1, not the new one
  //   Inpuy
  //   < Code
  //   , and .
endmodule

module ADD_SUB_1 (
  input  in_1,
  input  [7:0] in_2,
  output [7:0] out_3
);

  wire [7:0] xor_1_out;

  assign xor_1_out = {8{in_1}} ^ 8'h1;  // XOR_Gate xor_1, 8 bits wide
  Adder adder_1 (.a(in_2), .b(xor_1_out), .out(out_3), .cin(in_1));  // open: cout
endmodule

// Stack
module Stack_Memory (
  input  [7:0] Data_In,
  input  Write,
  input  Read,
  input  in_4,
  output [7:0] out_5
);

  wire or_1_out, or_2_out;
  wire [7:0] counter_1_q;

  or or_1 (or_1_out, Read, Write);
  Counter counter_1 (.load(Read), .count(or_1_out), .Q(counter_1_q), .clk(or_2_out), .clr(in_4));  // open: D, carry
  or or_2 (or_2_out, Read, Write);
  RAM #(.bus("separate")) ram_1 (
    .addr(counter_1_q), .din(Data_In), .data(out_5), .str(Write), .clk(or_2_out), .ld(Read), .clr(in_4));  // open: sel
endmodule
