// Logisim project IC CPU.circ as structural Verilog: 7 circuits, main circuit RAM
module RAM (
  input  A7,
  input  VDD,
  input  A6,
  input  A8,
  input  A5,
  input  A9,
  input  A4,
  input  minus_WE,
  input  A3,
  input  minus_OE,
  input  A2,
  input  A10,
  input  A1,
  input  CS,
  input  A0,
  input  D7,
  input  D0,
  input  D6,
  input  D1,
  input  D5,
  input  D2,
  input  D4,
  input  VSS,
  input  D3
);

  wire and_1_out, not_1_out, not_2_out, or_1_out, undriven;

  or or_1 (or_1_out, not_1_out, and_1_out);
  not not_1 (not_1_out, CS);
  RAM_part #(.addrWidth(11)) ram_1 (
    .addr({A10, A9, A8, A7, A6, A5, A4, A3, A2, A1, A0}), .data({D7, D6, D5, D4, D3, D2, D1, D0}),
    .sel(or_1_out), .clk(undriven), .ld(not_2_out));  // open: clr
  not not_2 (not_2_out, minus_WE);
  and and_1 (and_1_out, CS, minus_OE, minus_WE);
endmodule

// 16 x 4
module DM8599 (
  input  Vcc,
  input  A1,
  input  A2,
  input  A3,
  input  D4,
  input  D3,
  input  A0,
  input  ME,
  input  WE,
  input  D1,
  input  D2,
  input  GND,
  output S4,
  output S3,
  output S1,
  output S2
);

  wire and_1_out, and_2_out, not_1_out, not_2_out, not_3_out, not_5_out;
  wire [3:0] controlled_buffer_1_out, ram_1_data;

  and and_1 (and_1_out, not_1_out, not_2_out);
  and and_2 (and_2_out, not_3_out, WE);
  not not_1 (not_1_out, ME);
  not not_2 (not_2_out, WE);
  not not_3 (not_3_out, ME);
  RAM_part #(.addrWidth(4), .dataWidth(4), .bus("separate")) ram_1 (
    .addr({A3, A2, A1, A0}), .din({D4, D3, D2, D1}), .data(ram_1_data), .str(and_1_out), .clk(and_1_out));  // open: sel, ld, clr
  assign controlled_buffer_1_out = and_2_out ? ram_1_data : 4'bz;  // Controlled_Buffer controlled_buffer_1
  assign {S4, S3, S2, S1} = ~controlled_buffer_1_out;  // NOT_Gate not_4, 4 bits wide
  assign controlled_buffer_1_out = not_5_out ? 4'b1111 : 4'bz;  // Controlled_Buffer controlled_buffer_2
  not not_5 (not_5_out, and_2_out);
endmodule

module main (
  input  ME,
  input  WE,
  input  in_3,
  input  in_4,
  input  in_5,
  input  in_6,
  input  in_7,
  input  in_8,
  input  in_9,
  input  in_10,
  input  in_11,
  input  in_12,
  input  in_13,
  input  in_14,
  input  in_15,
  input  in_16,
  input  in_17,
  input  in_18,
  input  in_19,
  input  in_20,
  input  in_21,
  input  in_22,
  input  in_23,
  input  in_24,
  input  in_25,
  input  in_26,
  input  in_27,
  input  in_28,
  input  in_29,
  input  in_30
);

  wire A_q1, A_q2, A_q3, A_q4, B_q1, B_q2, B_q3, B_q4, clock_1_out, dm8599_1_s1, dm8599_1_s2, dm8599_1_s3,
       dm8599_1_s4, dm8599_2_s1, dm8599_2_s2, dm8599_2_s3, dm8599_2_s4, dm8599_3_s1, dm8599_3_s2,
       dm8599_3_s3, dm8599_3_s4, dm8599_4_s1, dm8599_4_s2, dm8599_4_s3, dm8599_4_s4, dm8599_5_s1,
       dm8599_5_s2, dm8599_5_s3, dm8599_5_s4, dm8599_6_s1, dm8599_6_s2, dm8599_6_s3, dm8599_6_s4,
       dm8599_7_s1, dm8599_7_s2, dm8599_7_s3, dm8599_7_s4, IR_q1, IR_q2, IR_q3, IR_q4, Memory_RAM_s1,
       Memory_RAM_s2, Memory_RAM_s3, Memory_RAM_s4, n7485_1_qa_b, n7485_1_qa_b_2, n7485_1_qa_b_3,
       n74157_1_p6, n74157_1_p7, n74157_1_p9, n74157_1_p11, n74157_1_p12, n74157_1_p14, n74157_1_p15,
       n74157_1_p17, not_1_out, not_2_out, not_3_out, not_4_out, not_5_out, not_6_out, not_7_out, not_8_out,
       not_9_out, not_10_out, not_11_out, not_12_out, not_13_out, not_14_out, not_15_out, not_16_out,
       not_17_out, not_18_out, not_19_out, not_20_out, not_21_out, not_22_out, not_23_out, not_24_out,
       not_25_out, not_26_out, not_27_out, not_28_out, not_29_out, not_30_out, not_31_out;
  wire [3:0] test_1_out_15;

  not not_1 (not_1_out, in_3);
  not not_2 (not_2_out, in_4);
  not not_3 (not_3_out, in_5);
  not not_4 (not_4_out, in_6);
  not not_5 (not_5_out, in_7);
  not not_6 (not_6_out, in_8);
  not not_7 (not_7_out, in_9);
  not not_8 (not_8_out, in_10);
  not not_9 (not_9_out, in_11);
  not not_10 (not_10_out, in_12);
  not not_11 (not_11_out, in_13);
  not not_12 (not_12_out, in_14);
  not not_13 (not_13_out, in_15);
  not not_14 (not_14_out, in_16);
  not not_15 (not_15_out, in_17);
  not not_16 (not_16_out, in_18);
  not not_17 (not_17_out, in_19);
  not not_18 (not_18_out, in_20);
  not not_19 (not_19_out, in_21);
  not not_20 (not_20_out, in_22);
  not not_21 (not_21_out, in_23);
  not not_22 (not_22_out, in_24);
  not not_23 (not_23_out, in_25);
  not not_24 (not_24_out, in_26);
  not not_25 (not_25_out, in_27);
  not not_26 (not_26_out, in_28);
  not not_27 (not_27_out, in_29);
  not not_28 (not_28_out, in_30);
  _74175 IR (
    .Q4(IR_q4), .D4(test_1_out_15[0]), .D3(test_1_out_15[1]), .Q3(IR_q3), .Clock(clock_1_out), .Q1(IR_q1),
    .D1(test_1_out_15[3]), .D2(test_1_out_15[2]), .Q2(IR_q2));  // open: Vcc, minus_Q4, minus_Q3, Clear, minus_Q1, minus_Q2, Gnd
  DM8599 dm8599_1 (
    .A1(IR_q2), .A2(IR_q4), .A3(IR_q4), .D4(not_4_out), .S4(dm8599_1_s4), .D3(not_3_out), .S3(dm8599_1_s3),
    .A0(IR_q1), .ME(ME), .WE(WE), .D1(not_1_out), .S1(dm8599_1_s1), .D2(not_2_out), .S2(dm8599_1_s2));  // open: Vcc, GND
  DM8599 dm8599_2 (
    .A1(IR_q2), .A2(IR_q4), .A3(IR_q4), .D4(not_8_out), .S4(dm8599_2_s4), .D3(not_7_out), .S3(dm8599_2_s3),
    .A0(IR_q1), .ME(ME), .WE(WE), .D1(not_5_out), .S1(dm8599_2_s1), .D2(not_6_out), .S2(dm8599_2_s2));  // open: Vcc, GND
  DM8599 dm8599_3 (
    .A1(IR_q2), .A2(IR_q4), .A3(IR_q4), .D4(not_12_out), .S4(dm8599_3_s4), .D3(not_11_out), .S3(dm8599_3_s3),
    .A0(IR_q1), .ME(ME), .WE(WE), .D1(not_9_out), .S1(dm8599_3_s1), .D2(not_10_out), .S2(dm8599_3_s2));  // open: Vcc, GND
  DM8599 dm8599_4 (
    .A1(IR_q2), .A2(IR_q3), .A3(IR_q4), .D4(not_16_out), .S4(dm8599_4_s4), .D3(not_15_out), .S3(dm8599_4_s3),
    .A0(IR_q1), .ME(ME), .WE(WE), .D1(not_13_out), .S1(dm8599_4_s1), .D2(not_14_out), .S2(dm8599_4_s2));  // open: Vcc, GND
  DM8599 dm8599_5 (
    .A1(IR_q2), .A2(IR_q3), .A3(IR_q4), .D4(not_20_out), .S4(dm8599_5_s4), .D3(not_19_out), .S3(dm8599_5_s3),
    .A0(IR_q1), .ME(ME), .WE(WE), .D1(not_17_out), .S1(dm8599_5_s1), .D2(not_18_out), .S2(dm8599_5_s2));  // open: Vcc, GND
  DM8599 dm8599_6 (
    .A1(IR_q2), .A2(IR_q3), .A3(IR_q4), .D4(not_24_out), .S4(dm8599_6_s4), .D3(not_23_out), .S3(dm8599_6_s3),
    .A0(IR_q1), .ME(ME), .WE(WE), .D1(not_21_out), .S1(dm8599_6_s1), .D2(not_22_out), .S2(dm8599_6_s2));  // open: Vcc, GND
  DM8599 dm8599_7 (
    .A1(IR_q2), .A2(IR_q3), .A3(IR_q4), .D4(not_28_out), .S4(dm8599_7_s4), .D3(not_27_out), .S3(dm8599_7_s3),
    .A0(IR_q1), .ME(ME), .WE(WE), .D1(not_25_out), .S1(dm8599_7_s1), .D2(not_26_out), .S2(dm8599_7_s2));  // open: Vcc, GND
  Clock clock_1 (.out(clock_1_out));
  // _74157 74157_1: pin names not known; wires that end beside it: 1'b0, dm8599_3_s3, dm8599_5_s4, dm8599_3_s2, dm8599_4_s4, n74157_1_p6, n74157_1_p7, dm8599_4_s3, n74157_1_p9, dm8599_3_s1, n74157_1_p11, n74157_1_p12, dm8599_4_s2, n74157_1_p14, n74157_1_p15, dm8599_4_s1, n74157_1_p17
  DM8599 Memory_RAM (
    .A1(dm8599_1_s2), .A2(dm8599_1_s3), .A3(dm8599_1_s4), .D4(n74157_1_p14), .S4(Memory_RAM_s4),
    .D3(n74157_1_p12), .S3(Memory_RAM_s3), .A0(dm8599_1_s1), .ME(dm8599_2_s4), .WE(dm8599_2_s3),
    .D1(n74157_1_p7), .S1(Memory_RAM_s1), .D2(n74157_1_p9), .S2(Memory_RAM_s2));  // open: Vcc, GND
  Test test_1 (
    .out_15(test_1_out_15), .IF(dm8599_7_s1), .IF_2(dm8599_7_s2), .IF_3(dm8599_7_s3), .IF_4(dm8599_7_s4),
    .ELSE(dm8599_6_s1), .ELSE_2(dm8599_6_s2), .ELSE_3(dm8599_6_s3), .ELSE_4(dm8599_6_s4), .in_9(dm8599_5_s1),
    .in_10(dm8599_5_s2), .in_11(dm8599_5_s3), .in_12(n7485_1_qa_b_3), .in_13(n7485_1_qa_b_2),
    .in_14(n7485_1_qa_b));
  _74175 A (
    .Q4(A_q4), .D4(Memory_RAM_s4), .D3(Memory_RAM_s3), .Q3(A_q3), .Clock(dm8599_2_s1), .Q1(A_q1),
    .D1(Memory_RAM_s1), .D2(Memory_RAM_s2), .Q2(A_q2));  // open: Vcc, minus_Q4, minus_Q3, Clear, minus_Q1, minus_Q2, Gnd
  _74175 B (
    .Q4(B_q4), .D4(Memory_RAM_s4), .D3(Memory_RAM_s3), .Q3(B_q3), .Clock(dm8599_2_s2), .Q1(B_q1),
    .D1(Memory_RAM_s1), .D2(Memory_RAM_s2), .Q2(B_q2));  // open: Vcc, minus_Q4, minus_Q3, Clear, minus_Q1, minus_Q2, Gnd
  not not_29 (not_29_out, dm8599_3_s4);
  not not_30 (not_30_out, dm8599_3_s4);
  not not_31 (not_31_out, dm8599_3_s4);
  _7485 u_7485_1 (
    .B3(B_q4), .QA_B(n7485_1_qa_b), .QA_B_2(n7485_1_qa_b_2), .QA_B_3(n7485_1_qa_b_3), .A3(A_q4), .B2(B_q3),
    .A2(A_q3), .A1(A_q2), .B1(B_q2), .A0(A_q1), .B0(B_q1));  // open: IA_B, IA_B_2, IA_B_3, Gnd, Vcc
  // _74181 74181_1: pin names not known; wires that end beside it: not_30_out, dm8599_3_s4, dm8599_3_s4, not_31_out, B_q4, A_q4, B_q3, A_q3, B_q2, A_q2, B_q1, A_q1, 1'b0, not_29_out, n74157_1_p17, n74157_1_p15, n74157_1_p11, n74157_1_p6

  // Notes on the sheet:
  //   Memory Needs to be updated
  //   ALU Functions:
  //   ADD: HLLH M=L Cn=H 
  //   SUB: LHHL M=L Cn=L
  //   :
endmodule

module Test (
  input  IF,
  input  IF_2,
  input  IF_3,
  input  IF_4,
  input  ELSE,
  input  ELSE_2,
  input  ELSE_3,
  input  ELSE_4,
  input  in_9,
  input  in_10,
  input  in_11,
  input  in_12,
  input  in_13,
  input  in_14,
  output [3:0] out_15
);

  wire and_1_out, and_2_out, and_3_out, or_1_out;

  Multiplexer #(.width(4)) multiplexer_1 (
    .in0({ELSE_4, ELSE_3, ELSE_2, ELSE}), .in1({IF_4, IF_3, IF_2, IF}), .out(out_15), .sel(or_1_out));  // open: en
  or or_1 (or_1_out, and_1_out, and_2_out, and_3_out);
  and and_1 (and_1_out, in_9, in_12);
  and and_2 (and_2_out, in_10, in_13);
  and and_3 (and_3_out, in_11, in_14);
endmodule

module adder (
  input  S3,
  input  S2,
  input  S1,
  input  S0,
  input  B3,
  input  A3,
  input  B2,
  input  A2,
  input  B1,
  input  A1,
  input  B0,
  input  A0,
  input  M,
  input  Cn,
  output G,
  output Cn_4,
  output P,
  output F3,
  output F2,
  output A_B,
  output F1,
  output F0
);

  wire and_1_out, and_2_out, and_3_out, and_4_out, and_5_out, and_6_out, and_7_out, and_8_out, and_9_out,
       and_10_out, and_11_out, and_12_out, and_13_out, and_14_out, and_15_out, and_16_out, and_17_out,
       and_18_out, and_19_out, and_20_out, and_21_out, and_22_out, and_23_out, and_24_out, and_25_out,
       and_26_out, and_28_out, and_29_out, and_30_out, and_31_out, and_32_out, and_33_out, and_34_out,
       and_35_out, and_36_out, and_37_out, and_38_out, nand_2_out, nand_4_out, nor_2_out, nor_3_out,
       nor_4_out, nor_5_out, nor_6_out, nor_7_out, nor_8_out, nor_9_out, nor_10_out, nor_11_out, nor_12_out,
       not_1_out, not_2_out, not_3_out, not_4_out, not_5_out, not_6_out, not_7_out, not_8_out, not_9_out;

  and and_1 (and_1_out, nor_3_out, nor_3_out);
  nor nor_1 (G, and_1_out, and_3_out, and_2_out, and_5_out, and_5_out);
  and and_2 (and_2_out, nor_2_out, nor_4_out, nor_9_out);
  and and_3 (and_3_out, nor_2_out, nor_6_out);
  nor nor_2 (nor_2_out, and_4_out, and_7_out);
  and and_4 (and_4_out, B3, S3, A3);
  nand nand_1 (Cn_4, G, nand_2_out);
  nand nand_2 (nand_2_out, nor_2_out, nor_4_out, nor_7_out, nor_11_out, Cn);
  and and_5 (and_5_out, nor_2_out, nor_4_out, nor_7_out, nor_12_out, nor_12_out);
  and and_6 (and_6_out, not_1_out, S1);
  and and_7 (and_7_out, A3, S2, not_1_out);
  not not_1 (not_1_out, B3);
  nand nand_3 (P, nor_2_out, nor_4_out, nor_7_out, nor_11_out, nor_11_out);
  nor nor_3 (nor_3_out, and_6_out, and_9_out, and_8_out);
  and and_8 (and_8_out, A3, A3);
  and and_9 (and_9_out, S0, B3);
  and and_10 (and_10_out, nor_2_out, not_2_out);
  not not_2 (not_2_out, nor_3_out);
  and and_11 (and_11_out, nor_4_out, nor_7_out, nor_11_out, Cn, not_9_out);
  nor nor_4 (nor_4_out, and_12_out, and_13_out);
  and and_12 (and_12_out, B2, S3, A2);
  and and_13 (and_13_out, A2, S2, not_3_out);
  not not_3 (not_3_out, B2);
  xor xor_1 (F3, and_10_out, nor_5_out);
  nor nor_5 (nor_5_out, and_11_out, and_15_out, and_14_out, and_19_out, and_19_out);
  and and_14 (and_14_out, nor_4_out, nor_9_out, not_9_out);
  and and_15 (and_15_out, nor_4_out, nor_7_out, Cn, not_9_out, not_9_out);
  nor nor_6 (nor_6_out, and_17_out, and_16_out, and_20_out);
  and and_16 (and_16_out, S0, B2);
  and and_17 (and_17_out, not_3_out, S1);
  and and_18 (and_18_out, nor_4_out, not_4_out);
  and and_19 (and_19_out, nor_6_out, not_9_out);
  and and_20 (and_20_out, A2, A2);
  and and_21 (and_21_out, nor_7_out, nor_7_out, nor_11_out, Cn, not_9_out);
  not not_4 (not_4_out, nor_6_out);
  nor nor_7 (nor_7_out, and_23_out, and_22_out);
  and and_22 (and_22_out, A1, S2, not_5_out);
  and and_23 (and_23_out, B1, S3, A1);
  xor xor_2 (F2, and_18_out, nor_8_out);
  nor nor_8 (nor_8_out, and_21_out, and_25_out, and_24_out);
  and and_24 (and_24_out, nor_9_out, not_9_out);
  and and_25 (and_25_out, nor_7_out, nor_12_out, not_9_out);
  and and_26 (and_26_out, not_5_out, S1);
  not not_5 (not_5_out, B1);
  and and_27 (A_B, F3, F3, F2, F1, F0);
  and and_28 (and_28_out, nor_7_out, not_6_out);
  not not_6 (not_6_out, nor_9_out);
  nor nor_9 (nor_9_out, and_26_out, and_30_out, and_29_out);
  and and_29 (and_29_out, A1, A1);
  and and_30 (and_30_out, S0, B1);
  xor xor_3 (F1, and_28_out, nor_10_out);
  nor nor_10 (nor_10_out, and_31_out, and_33_out);
  and and_31 (and_31_out, Cn, nor_11_out, not_9_out);
  nor nor_11 (nor_11_out, and_32_out, and_35_out);
  and and_32 (and_32_out, B0, S3, A0);
  and and_33 (and_33_out, nor_12_out, not_9_out);
  and and_34 (and_34_out, not_7_out, S1);
  and and_35 (and_35_out, A0, S2, not_7_out);
  not not_7 (not_7_out, B0);
  and and_36 (and_36_out, nor_11_out, not_8_out);
  not not_8 (not_8_out, nor_12_out);
  nor nor_12 (nor_12_out, and_34_out, and_38_out, and_37_out);
  and and_37 (and_37_out, A0, A0);
  and and_38 (and_38_out, S0, B0);
  xor xor_4 (F0, and_36_out, nand_4_out);
  nand nand_4 (nand_4_out, not_9_out, Cn);
  not not_9 (not_9_out, M);

  // Notes on the sheet:
  //   ADD: HLLH M=L Cn=H 
  //   SUB: LHHL M=L Cn=L
endmodule

module _7485 (
  input  B3,
  input  Vcc,
  input  IA_B,
  input  A3,
  input  IA_B_2,
  input  B2,
  input  IA_B_3,
  input  A2,
  input  A1,
  input  B1,
  input  A0,
  input  Gnd,
  input  B0,
  output QA_B,
  output QA_B_2,
  output QA_B_3
);

  Comparator #(.width(4)) comparator_1 (
    .a({A3, A2, A1, A0}), .b({B3, B2, B1, B0}), .gt(QA_B_3), .eq(QA_B_2), .lt(QA_B));
endmodule

module RAM2 (
  input  [7:0] Store_Data,
  input  [7:0] in_2,
  input  in_3,
  input  in_4,
  input  in_5,
  input  in_6,
  input  in_7
);

  wire controlled_buffer_1_out, controlled_buffer_2_out, not_1_out, not_2_out, not_3_out, ram_1_data,
       shift_register_1_out, shift_register_2_out, shift_register_2_q0, shift_register_2_q1,
       shift_register_2_q2, shift_register_2_q3, shift_register_2_q4, shift_register_2_q5,
       shift_register_2_q6, shift_register_2_q7, shift_register_3_out, shift_register_4_q0,
       shift_register_4_q1, shift_register_4_q2, shift_register_4_q3, shift_register_4_q4,
       shift_register_4_q5, shift_register_4_q6, shift_register_4_q7, undriven, undriven_2, undriven_3,
       undriven_4;
  wire [9:0] counter_1_q;

  assign controlled_buffer_1_out = undriven ? in_5 : 1'bz;  // Controlled_Buffer controlled_buffer_1
  not not_1 (not_1_out, in_4);
  assign controlled_buffer_2_out = not_1_out ? in_5 : 1'bz;  // Controlled_Buffer controlled_buffer_2
  Counter #(.width(10), .max('h3ff)) counter_1 (
    .load(in_6), .count(in_7), .Q(counter_1_q), .clk(controlled_buffer_2_out));  // open: D, carry, clr
  not not_2 (not_2_out, in_4);
  Shift_Register shift_register_1 (
    .shift(not_2_out), .clk(controlled_buffer_1_out), .out(shift_register_1_out), .load(in_4),
    .d0(Store_Data[7]), .d1(Store_Data[6]), .d2(Store_Data[5]), .d3(Store_Data[4]), .d4(Store_Data[3]),
    .d5(Store_Data[2]), .d6(Store_Data[1]), .d7(Store_Data[0]));  // open: in, clr, q0, q1, q2, q3, q4, q5, q6, q7
  Shift_Register shift_register_2 (
    .in(ram_1_data), .clk(undriven_2), .out(shift_register_2_out), .q0(shift_register_2_q0),
    .q1(shift_register_2_q1), .q2(shift_register_2_q2), .q3(shift_register_2_q3), .q4(shift_register_2_q4),
    .q5(shift_register_2_q5), .q6(shift_register_2_q6), .q7(shift_register_2_q7));  // open: shift, load, clr, d0, d1, d2, d3, d4, d5, d6, d7
  not not_3 (not_3_out, in_4);
  Shift_Register shift_register_3 (
    .shift(not_3_out), .in(shift_register_1_out), .clk(controlled_buffer_1_out), .out(shift_register_3_out),
    .load(in_4), .d0(in_2[7]), .d1(in_2[6]), .d2(in_2[5]), .d3(in_2[4]), .d4(in_2[3]), .d5(in_2[2]),
    .d6(in_2[1]), .d7(in_2[0]));  // open: clr, q0, q1, q2, q3, q4, q5, q6, q7
  RAM_part #(.addrWidth(10), .dataWidth(1), .bus("separate")) ram_1 (
    .addr(counter_1_q), .din(shift_register_3_out), .data(ram_1_data), .str(undriven_3),
    .clk(controlled_buffer_2_out), .ld(undriven_4));  // open: sel, clr
  Shift_Register shift_register_4 (
    .in(shift_register_2_out), .clk(undriven_2), .q0(shift_register_4_q0), .q1(shift_register_4_q1),
    .q2(shift_register_4_q2), .q3(shift_register_4_q3), .q4(shift_register_4_q4), .q5(shift_register_4_q5),
    .q6(shift_register_4_q6), .q7(shift_register_4_q7));  // open: shift, out, load, clr, d0, d1, d2, d3, d4, d5, d6, d7

  // Notes on the sheet:
  //   Load Data to Output
endmodule
