// Logisim project Non BF Computer.circ as structural Verilog: 1 circuit, main circuit main
module main (
);

  wire and_1_out, clock_1_out, comparator_1_eq, decoder_1_out1, decoder_1_out3, decoder_1_out4,
       decoder_1_out5, decoder_1_out6, decoder_1_out7, decoder_1_out8, decoder_1_out9, decoder_1_out10,
       decoder_1_out11, decoder_1_out12, not_1_out, or_1_out, or_2_out, or_3_out, or_4_out, or_5_out,
       or_6_out, or_7_out;
  wire [7:0] adder_1_out, keyboard_1_data, multiplexer_1_out, multiplexer_2_out, ram_2_data, register_1_q,
       register_2_q, register_3_q, register_4_q, xor_1_out;
  wire [7:7] decoder_1_out2;
  wire [11:0] ram_1_data;
  wire [15:0] counter_1_q;

  Register register_1 (.D(ram_1_data[7:0]), .Q(register_1_q), .clk(decoder_1_out9));  // open: en, clr
  Register register_2 (.D(ram_1_data[7:0]), .Q(register_2_q), .clk(decoder_1_out10));  // open: en, clr
  Counter #(.width(16), .max('hffff)) counter_1 (
    .load(or_4_out), .D({register_1_q, register_2_q}), .count(not_1_out), .Q(counter_1_q), .clk(clock_1_out));  // open: carry, clr
  not not_1 (not_1_out, or_4_out);
  Clock clock_1 (.out(clock_1_out));
  RAM #(.addrWidth(16), .dataWidth(12), .bus("separate")) ram_1 (
    .addr(counter_1_q), .data(ram_1_data), .clk(clock_1_out));  // open: din, str, sel, ld, clr
  Decoder #(.select(4)) decoder_1 (
    .out1(decoder_1_out1), .out2(decoder_1_out2[7]), .out3(decoder_1_out3), .out4(decoder_1_out4),
    .out5(decoder_1_out5), .out6(decoder_1_out6), .out7(decoder_1_out7), .out8(decoder_1_out8),
    .out9(decoder_1_out9), .out10(decoder_1_out10), .out11(decoder_1_out11), .out12(decoder_1_out12),
    .sel(ram_1_data[11:8]));  // open: out0, out13, out14, out15, en
  or or_1 (or_1_out, decoder_1_out1, decoder_1_out2[7], decoder_1_out12, decoder_1_out7);
  or or_2 (or_2_out, decoder_1_out1, decoder_1_out2[7], decoder_1_out12);
  RAM #(.bus("separate")) ram_2 (
    .addr(ram_1_data[7:0]), .din(multiplexer_2_out), .data(ram_2_data), .str(or_2_out), .clk(or_1_out),
    .ld(or_3_out));  // open: sel, clr
  or or_3 (or_3_out, decoder_1_out5, decoder_1_out6, decoder_1_out7);
  or or_4 (or_4_out, decoder_1_out8, and_1_out);
  Multiplexer #(.width(8)) multiplexer_1 (
    .in0(ram_2_data), .in1(ram_1_data[7:0]), .out(multiplexer_1_out), .en(or_5_out));  // open: sel
  or or_5 (or_5_out, decoder_1_out3, decoder_1_out4);
  and and_1 (and_1_out, decoder_1_out7, comparator_1_eq);
  Register register_3 (.D(multiplexer_1_out), .Q(register_3_q), .clk(or_6_out));  // open: en, clr
  Register register_4 (.D(multiplexer_1_out), .Q(register_4_q), .clk(or_7_out));  // open: en, clr
  or or_6 (or_6_out, decoder_1_out3, decoder_1_out5);
  or or_7 (or_7_out, decoder_1_out4, decoder_1_out6);
  Comparator #(.mode("unsigned")) comparator_1 (
    .a(multiplexer_1_out), .b({8{1'b0}}), .eq(comparator_1_eq));  // open: gt, lt
  assign xor_1_out = register_3_q ^ {8{decoder_1_out2[7]}};  // XOR_Gate xor_1, 8 bits wide
  Adder adder_1 (.a(xor_1_out), .b(register_4_q), .out(adder_1_out), .cin(decoder_1_out2[7]));  // open: cout
  TTY tty_1 (.data(ram_2_data[6:0]), .clk(decoder_1_out11));  // open: we, clr
  Keyboard keyboard_1 (.clk(decoder_1_out12), .data(keyboard_1_data[6:0]));  // open: re, clr, avail
  Multiplexer #(.width(8)) multiplexer_2 (
    .in0(adder_1_out), .in1(keyboard_1_data), .out(multiplexer_2_out), .en(decoder_1_out12));  // open: sel

  // Notes on the sheet:
  //   To Jump:
  //   If Statement
  //   1) Load first 8 address digits
  //   2) Load second 8 address digits
  //   3) Load to 16 bit address register
  //   1) Load first 8 address digits
  //   2) Load second 8 address digits
  //   3) If ram == 0: Load 16 bit address register
  //   Make it so that certain commands are connected to load on the ram and others are connected to store on the ram
  //   Depending on timing, jump and if may be able to be confined to two clock cycles: 1) Load first 8 digits 2) load second 8 digits and jump
  //   The jump statement may be able to be conjoined with the if statement. It could simply be an if statement that loads a non-zero number into the mux so it always jumps
endmodule
