// Logisim project SR memory.circ as structural Verilog: 4 circuits, main circuit main
module main (
  input  in_1,
  input  in_2,
  input  in_3,
  input  in_4,
  input  Address,
  input  in_6,
  input  in_7,
  input  in_8
);

  wire controlled_buffer_1_out, controlled_buffer_2_out, controlled_buffer_3_out, controlled_buffer_4_out,
       controlled_buffer_5_out, controlled_buffer_6_out, controlled_buffer_7_out, controlled_buffer_8_out,
       controlled_buffer_9_out, controlled_buffer_10_out, controlled_buffer_11_out, controlled_buffer_12_out,
       controlled_buffer_13_out, controlled_buffer_14_out, controlled_buffer_15_out,
       controlled_buffer_16_out, not_1_out, not_2_out, not_3_out, not_4_out, not_5_out, not_6_out, not_7_out,
       not_8_out, not_9_out, not_10_out, not_11_out, not_12_out, not_13_out, not_14_out, not_15_out,
       not_16_out, register_1_out_16, register_1_out_18, register_1_out_20, register_1_out_22,
       register_2_out_16, register_2_out_18, register_2_out_20, register_2_out_22, register_3_out_16,
       register_3_out_18, register_3_out_20, register_3_out_22, register_4_out_16, register_4_out_18,
       register_4_out_20, register_4_out_22;

  Register register_1 (
    .in_1(controlled_buffer_1_out), .out_16(register_1_out_16), .in_3(not_1_out),
    .in_4(controlled_buffer_2_out), .out_18(register_1_out_18), .in_6(not_2_out),
    .in_7(controlled_buffer_3_out), .out_20(register_1_out_20), .in_9(not_3_out),
    .in_10(controlled_buffer_4_out), .out_22(register_1_out_22), .in_12(not_4_out));  // open: in_2, out_17, in_5, out_19, in_8, out_21, in_11, out_23, in_13, out_24, in_14, out_25, in_15
  not not_1 (not_1_out, controlled_buffer_1_out);
  assign controlled_buffer_1_out = Address ? in_1 : 1'bz;  // Controlled_Buffer controlled_buffer_1
  assign controlled_buffer_2_out = Address ? in_2 : 1'bz;  // Controlled_Buffer controlled_buffer_2
  not not_2 (not_2_out, controlled_buffer_2_out);
  not not_3 (not_3_out, controlled_buffer_3_out);
  assign controlled_buffer_3_out = Address ? in_3 : 1'bz;  // Controlled_Buffer controlled_buffer_3
  not not_4 (not_4_out, controlled_buffer_4_out);
  assign controlled_buffer_4_out = Address ? in_4 : 1'bz;  // Controlled_Buffer controlled_buffer_4
  Register register_2 (
    .in_1(controlled_buffer_5_out), .out_16(register_2_out_16), .in_3(not_5_out),
    .in_4(controlled_buffer_6_out), .out_18(register_2_out_18), .in_6(not_6_out),
    .in_7(controlled_buffer_7_out), .out_20(register_2_out_20), .in_9(not_7_out),
    .in_10(controlled_buffer_8_out), .out_22(register_2_out_22), .in_12(not_8_out));  // open: in_2, out_17, in_5, out_19, in_8, out_21, in_11, out_23, in_13, out_24, in_14, out_25, in_15
  assign controlled_buffer_5_out = in_6 ? in_1 : 1'bz;  // Controlled_Buffer controlled_buffer_5
  not not_5 (not_5_out, controlled_buffer_5_out);
  assign controlled_buffer_6_out = in_6 ? in_2 : 1'bz;  // Controlled_Buffer controlled_buffer_6
  not not_6 (not_6_out, controlled_buffer_6_out);
  not not_7 (not_7_out, controlled_buffer_7_out);
  assign controlled_buffer_7_out = in_6 ? in_3 : 1'bz;  // Controlled_Buffer controlled_buffer_7
  assign controlled_buffer_8_out = in_6 ? in_4 : 1'bz;  // Controlled_Buffer controlled_buffer_8
  not not_8 (not_8_out, controlled_buffer_8_out);
  Register register_3 (
    .in_1(controlled_buffer_9_out), .out_16(register_3_out_16), .in_3(not_9_out),
    .in_4(controlled_buffer_10_out), .out_18(register_3_out_18), .in_6(not_10_out),
    .in_7(controlled_buffer_11_out), .out_20(register_3_out_20), .in_9(not_11_out),
    .in_10(controlled_buffer_12_out), .out_22(register_3_out_22), .in_12(not_12_out));  // open: in_2, out_17, in_5, out_19, in_8, out_21, in_11, out_23, in_13, out_24, in_14, out_25, in_15
  assign controlled_buffer_9_out = in_7 ? in_1 : 1'bz;  // Controlled_Buffer controlled_buffer_9
  not not_9 (not_9_out, controlled_buffer_9_out);
  not not_10 (not_10_out, controlled_buffer_10_out);
  assign controlled_buffer_10_out = in_7 ? in_2 : 1'bz;  // Controlled_Buffer controlled_buffer_10
  assign controlled_buffer_11_out = in_7 ? in_3 : 1'bz;  // Controlled_Buffer controlled_buffer_11
  not not_11 (not_11_out, controlled_buffer_11_out);
  assign controlled_buffer_12_out = in_7 ? in_4 : 1'bz;  // Controlled_Buffer controlled_buffer_12
  not not_12 (not_12_out, controlled_buffer_12_out);
  Register register_4 (
    .in_1(controlled_buffer_13_out), .out_16(register_4_out_16), .in_3(not_13_out),
    .in_4(controlled_buffer_14_out), .out_18(register_4_out_18), .in_6(not_14_out),
    .in_7(controlled_buffer_15_out), .out_20(register_4_out_20), .in_9(not_15_out),
    .in_10(controlled_buffer_16_out), .out_22(register_4_out_22), .in_12(not_16_out));  // open: in_2, out_17, in_5, out_19, in_8, out_21, in_11, out_23, in_13, out_24, in_14, out_25, in_15
  not not_13 (not_13_out, controlled_buffer_13_out);
  assign controlled_buffer_13_out = in_8 ? in_1 : 1'bz;  // Controlled_Buffer controlled_buffer_13
  not not_14 (not_14_out, controlled_buffer_14_out);
  assign controlled_buffer_14_out = in_8 ? in_2 : 1'bz;  // Controlled_Buffer controlled_buffer_14
  assign controlled_buffer_15_out = in_8 ? in_3 : 1'bz;  // Controlled_Buffer controlled_buffer_15
  not not_15 (not_15_out, controlled_buffer_15_out);
  not not_16 (not_16_out, controlled_buffer_16_out);
  assign controlled_buffer_16_out = in_8 ? in_4 : 1'bz;  // Controlled_Buffer controlled_buffer_16
  Controlled_Buffer controlled_buffer_17 (.in(register_4_out_22), .en(in_8));  // open: out
  Controlled_Buffer controlled_buffer_18 (.in(register_3_out_22), .en(in_7));  // open: out
  Controlled_Buffer controlled_buffer_19 (.in(register_2_out_22), .en(in_6));  // open: out
  Controlled_Buffer controlled_buffer_20 (.in(register_1_out_22), .en(Address));  // open: out
  Controlled_Buffer controlled_buffer_21 (.in(register_4_out_16), .en(in_8));  // open: out
  Controlled_Buffer controlled_buffer_22 (.in(register_4_out_18), .en(in_8));  // open: out
  Controlled_Buffer controlled_buffer_23 (.in(register_4_out_20), .en(in_8));  // open: out
  Controlled_Buffer controlled_buffer_24 (.in(register_3_out_16), .en(in_7));  // open: out
  Controlled_Buffer controlled_buffer_25 (.in(register_3_out_18), .en(in_7));  // open: out
  Controlled_Buffer controlled_buffer_26 (.in(register_3_out_20), .en(in_7));  // open: out
  Controlled_Buffer controlled_buffer_27 (.in(register_2_out_16), .en(in_6));  // open: out
  Controlled_Buffer controlled_buffer_28 (.in(register_2_out_18), .en(in_6));  // open: out
  Controlled_Buffer controlled_buffer_29 (.in(register_2_out_20), .en(in_6));  // open: out
  Controlled_Buffer controlled_buffer_30 (.in(register_1_out_16), .en(Address));  // open: out
  Controlled_Buffer controlled_buffer_31 (.in(register_1_out_18), .en(Address));  // open: out
  Controlled_Buffer controlled_buffer_32 (.in(register_1_out_20), .en(Address));  // open: out
  // OR_Gate or_1 is placed but not wired
  // OR_Gate or_2 is placed but not wired
  // OR_Gate or_3 is placed but not wired
  // OR_Gate or_4 is placed but not wired

  // Other names for the same wires on the sheet: A = in_1; B = in_2; C = in_3; D = in_4

  // Notes on the sheet:
  //   Data
endmodule

module Register (
  input  in_1,
  input  in_2,
  input  in_3,
  input  in_4,
  input  in_5,
  input  in_6,
  input  in_7,
  input  in_8,
  input  in_9,
  input  in_10,
  input  in_11,
  input  in_12,
  input  in_13,
  input  in_14,
  input  in_15,
  output out_16,
  output out_17,
  output out_18,
  output out_19,
  output out_20,
  output out_21,
  output out_22,
  output out_23,
  output out_24,
  output out_25
);

  S_R_Flip_Flop s_r_ff_1 (.Q(out_16), .Qn(out_17), .preset(in_1), .reset(in_3));  // open: S, clk, R, en
  S_R_Flip_Flop s_r_ff_2 (.Q(out_18), .Qn(out_19), .preset(in_4), .reset(in_6));  // open: S, clk, R, en
  S_R_Flip_Flop s_r_ff_3 (.Q(out_20), .Qn(out_21), .preset(in_7), .reset(in_9));  // open: S, clk, R, en
  S_R_Flip_Flop s_r_ff_4 (.Q(out_22), .Qn(out_23), .preset(in_10), .reset(in_12));  // open: S, clk, R, en
  S_R_Flip_Flop s_r_ff_5 (.Q(out_24), .Qn(out_25), .preset(in_13), .reset(in_15));  // open: S, clk, R, en

  // Notes on the sheet:
  //   Power is replaced by output for logisim. In real life the output pins are for power and the input pins are for both input and output
endmodule

module D_latch (
  input  in_1,
  input  in_2,
  input  in_3,
  input  in_4,
  input  in_5,
  input  in_6,
  output out_7,
  output out_8,
  output out_9,
  output out_10,
  output out_11,
  output out_12
);

  wire and_1_out, and_2_out, and_3_out, undriven;

  S_R_Flip_Flop s_r_ff_1 (.Q(out_7), .Qn(out_10), .preset(and_1_out), .reset(and_2_out));  // open: S, clk, R, en
  and and_1 (and_1_out, in_3, in_4);
  and and_2 (and_2_out, ~in_3, in_4);  // AND_Gate
  D_Flip_Flop d_ff_1 (.clk(in_1), .D(in_2), .Q(out_8), .Qn(out_11));  // open: preset, en, reset
  S_R_Flip_Flop s_r_ff_2 (.Q(out_9), .Qn(out_12), .preset(and_3_out), .reset(undriven));  // open: S, clk, R, en
  and and_3 (and_3_out, in_5, in_6);
endmodule

module Relay___not (
  input  Data,
  input  Control,
  output Relay,
  output NOT
);

  assign Relay = Control ? Data : 1'bz;  // Controlled_Buffer controlled_buffer_1
  not not_1 (NOT, Relay);
endmodule
