// Logisim project 74175(register).circ as structural Verilog: 1 circuit, main circuit 74175
module _74175 (
  input  Vcc,
  input  D4,
  input  D3,
  input  Clock,
  input  Clear,
  input  D1,
  input  D2,
  input  Gnd,
  output Q4,
  output minus_Q4,
  output Q3,
  output minus_Q3,
  output Q1,
  output minus_Q1,
  output Q2,
  output minus_Q2
);

  wire not_1_out;

  not not_1 (not_1_out, Clear);
  D_Flip_Flop d_ff_1 (.clk(Clock), .D(D4), .Q(Q4), .Qn(minus_Q4), .reset(not_1_out));  // open: preset, en
  D_Flip_Flop d_ff_2 (.clk(Clock), .D(D1), .Q(Q1), .Qn(minus_Q1), .reset(not_1_out));  // open: preset, en
  D_Flip_Flop d_ff_3 (.clk(Clock), .D(D3), .Q(Q3), .Qn(minus_Q3), .reset(not_1_out));  // open: preset, en
  D_Flip_Flop d_ff_4 (.clk(Clock), .D(D2), .Q(Q2), .Qn(minus_Q2), .reset(not_1_out));  // open: preset, en
endmodule
