// Logisim project 74189.circ as structural Verilog: 1 circuit, main circuit 74189
module _74189 (
  input  S3,
  input  GND,
  input  S2,
  input  S4,
  input  S1,
  input  A3,
  input  A2,
  input  WE,
  input  A1,
  input  ME,
  input  Vcc,
  input  A0,
  output D3,
  output D2,
  output D4,
  output D1
);

  wire not_1_out;

  not not_1 (not_1_out, WE);
  RAM #(.addrWidth(4), .dataWidth(4), .bus("separate")) ram_1 (
    .addr({A3, A2, A1, A0}), .din({S4, S3, S2, S1}), .data({D4, D3, D2, D1}), .str(not_1_out), .clk(WE),
    .ld(WE));  // open: sel, clr
endmodule
