// Logisim project microcomputer.circ as structural Verilog: 10 circuits, main circuit main
module main (
  input  in_1,
  input  in_2,
  output [7:0] out_3
);

  wire alu_1_out_5, alu_1_out_6, alu_1_out_7, clock_1_out, R_out;
  wire [3:0] counter_1_q, test_1_out_9;
  wire [7:0] multiplexer_1_out, ram_1_data, register_1_q, register_2_q;
  wire [31:0] rom_1_data;

  Counter #(.width(4), .max('hf)) counter_1 (
    .load(in_1), .D(test_1_out_9), .count(in_2), .Q(counter_1_q), .clk(clock_1_out));  // open: carry, clr
  Clock clock_1 (.out(clock_1_out));
  Button R (.out(R_out));
  Multiplexer #(.width(8)) multiplexer_1 (
    .in0(out_3), .in1(rom_1_data[19:12]), .out(multiplexer_1_out), .sel(rom_1_data[11]));  // open: en
  ROM #(.addrWidth(4), .dataWidth(32)) rom_1 (.addr(counter_1_q), .data(rom_1_data));  // open: sel
  Test test_1 (
    .out_9(test_1_out_9), .IF_TRUE(rom_1_data[3:0]), .IF_NOT(rom_1_data[7:4]), .in_3(rom_1_data[8]),
    .in_4(rom_1_data[9]), .in_5(rom_1_data[10]), .in_6(alu_1_out_5), .in_7(alu_1_out_6), .in_8(alu_1_out_7));
  RAM #(.addrWidth(4), .bus("separate")) ram_1 (
    .addr(rom_1_data[31:28]), .din(multiplexer_1_out), .data(ram_1_data), .str(rom_1_data[27]),
    .clk(rom_1_data[26]), .ld(rom_1_data[25]), .clr(R_out));  // open: sel
  Register #(.trigger("high")) register_1 (.D(ram_1_data), .Q(register_1_q), .clk(rom_1_data[24]));  // open: en, clr
  Register #(.trigger("high")) register_2 (.D(ram_1_data), .Q(register_2_q), .clk(rom_1_data[23]));  // open: en, clr
  ALU alu_1 (
    .A_input(register_1_q), .B_input(register_2_q), .in_1(rom_1_data[22:20]), .Output(out_3),
    .out_5(alu_1_out_5), .out_6(alu_1_out_6), .out_7(alu_1_out_7));

  // Notes on the sheet:
  //   Count By Blank:
  //   00001100  C
  //   01001010  4a
  //   00110000  30
  //   contents of rom_1 (hex, n*v repeats v):
  //   4c001810 7100020 16900030 16f c010040 37100050 47100060 3c000070 10 37100080 76900090 c0000a0 b0
endmodule

module Adder_Subtractor (
  input  A_S,
  input  [3:0] A,
  input  [3:0] B,
  output [3:0] Output
);

  wire [3:0] xor_1_out;

  assign xor_1_out = {4{A_S}} ^ A;  // XOR_Gate xor_1, 4 bits wide
  Adder #(.width(4)) adder_1 (.a(xor_1_out), .b(B), .out(Output), .cin(A_S));  // open: cout
endmodule

module circuit (
  input  a,
  input  b,
  output a_2,
  output b_2
);

  wire and_2_out, and_3_out, not_1_out, not_2_out, not_3_out;

  not not_1 (not_1_out, b);
  not not_2 (not_2_out, a);
  not not_3 (not_3_out, b);
  and and_1 (a_2, a, not_1_out);
  and and_2 (and_2_out, not_2_out, b);
  and and_3 (and_3_out, a, not_3_out);
  or or_1 (b_2, and_2_out, and_3_out);
endmodule

module ALU (
  input  [2:0] in_1,
  input  [7:0] A_input,
  input  [7:0] B_input,
  output [7:0] Output,
  output out_5,
  output out_6,
  output out_7
);

  wire [7:0] adder_1_out, and_1_out, demultiplexer_1_out0, demultiplexer_1_out1, demultiplexer_1_out2,
       demultiplexer_1_out3, demultiplexer_1_out4, demultiplexer_1_out5, demultiplexer_2_out0,
       demultiplexer_2_out1, demultiplexer_2_out2, demultiplexer_2_out3, demultiplexer_2_out4,
       demultiplexer_2_out5, divider_1_out, multiplier_1_out, or_1_out, subtractor_1_out;

  Demultiplexer #(.select(3), .width(8)) demultiplexer_1 (
    .out0(demultiplexer_1_out0), .out1(demultiplexer_1_out1), .out2(demultiplexer_1_out2),
    .out3(demultiplexer_1_out3), .out4(demultiplexer_1_out4), .out5(demultiplexer_1_out5), .in(A_input),
    .sel(in_1));  // open: out6, out7, en
  Demultiplexer #(.select(3), .width(8)) demultiplexer_2 (
    .out0(demultiplexer_2_out0), .out1(demultiplexer_2_out1), .out2(demultiplexer_2_out2),
    .out3(demultiplexer_2_out3), .out4(demultiplexer_2_out4), .out5(demultiplexer_2_out5), .in(B_input),
    .sel(in_1));  // open: out6, out7, en
  Adder adder_1 (.a(demultiplexer_1_out0), .b(demultiplexer_2_out0), .out(adder_1_out));  // open: cin, cout
  Subtractor subtractor_1 (
    .a(demultiplexer_1_out1), .b(demultiplexer_2_out1), .out(subtractor_1_out));  // open: bin, bout
  Multiplier multiplier_1 (
    .a(demultiplexer_1_out2), .b(demultiplexer_2_out2), .out(multiplier_1_out));  // open: cin, cout
  Divider divider_1 (.a(demultiplexer_1_out3), .b(demultiplexer_2_out3), .out(divider_1_out));  // open: upper, rem
  assign and_1_out = demultiplexer_1_out4 & demultiplexer_2_out4;  // AND_Gate and_1, 8 bits wide
  assign or_1_out = demultiplexer_1_out5 | demultiplexer_2_out5;  // OR_Gate or_1, 8 bits wide
  Comparator comparator_1 (.a(A_input), .b(B_input), .gt(out_5), .eq(out_6), .lt(out_7));
  Multiplexer #(.select(3), .width(8)) multiplexer_1 (
    .in0(adder_1_out), .in1(subtractor_1_out), .in2(multiplier_1_out), .in3(divider_1_out), .in4(and_1_out),
    .in5(or_1_out), .out(Output), .sel(in_1));  // open: in6, in7, en
endmodule

module Test (
  input  [3:0] IF_TRUE,
  input  [3:0] IF_NOT,
  input  in_3,
  input  in_4,
  input  in_5,
  input  in_6,
  input  in_7,
  input  in_8,
  output [3:0] out_9
);

  wire and_1_out, and_2_out, and_3_out, or_1_out;

  Multiplexer #(.width(4)) multiplexer_1 (.in0(IF_NOT), .in1(IF_TRUE), .out(out_9), .sel(or_1_out));  // open: en
  or or_1 (or_1_out, and_1_out, and_2_out, and_3_out);
  and and_1 (and_1_out, in_3, in_6);
  and and_2 (and_2_out, in_4, in_7);
  and and_3 (and_3_out, in_5, in_8);
endmodule

module Mark_1 (
  input  b,
  input  [3:0] in_2,
  output [3:0] out_3
);

  wire and_1_out, and_2_out, clock_1_out, comparator_1_eq, not_1_out, not_2_out;
  wire [3:0] counter_1_q, ram_1_data, register_1_q, register_2_q;
  wire [7:0] rom_1_data;

  and and_1 (and_1_out, comparator_1_eq, not_1_out);
  not not_1 (not_1_out, b);
  not not_2 (not_2_out, comparator_1_eq);
  and and_2 (and_2_out, not_2_out, b);
  Counter #(.width(4), .max('hf)) counter_1 (
    .load(and_1_out), .count(and_2_out), .Q(counter_1_q), .clk(clock_1_out));  // open: D, carry, clr
  Clock clock_1 (.out(clock_1_out));
  Comparator #(.width(4)) comparator_1 (.a(counter_1_q), .b(in_2), .eq(comparator_1_eq));  // open: gt, lt
  ROM #(.addrWidth(4)) rom_1 (.addr(counter_1_q), .data(rom_1_data));  // open: sel
  RAM #(.addrWidth(2), .dataWidth(4), .bus("separate")) ram_1 (
    .addr(rom_1_data[7:6]), .din(out_3), .data(ram_1_data), .str(rom_1_data[5]), .clk(rom_1_data[4]),
    .ld(rom_1_data[3]));  // open: sel, clr
  Register #(.width(4), .trigger("high")) register_1 (
    .D(ram_1_data), .Q(register_1_q), .clk(rom_1_data[2]));  // open: en, clr
  Register #(.width(4), .trigger("high")) register_2 (
    .D(ram_1_data), .Q(register_2_q), .clk(rom_1_data[1]));  // open: en, clr
  Adder_Subtractor Adder_Subtractor (.A_S(rom_1_data[0]), .A(register_1_q), .B(register_2_q), .Output(out_3));

  // Notes on the sheet:
  //   Count By Blank:
  //   00001100  C
  //   01001010  4a
  //   00110000  30
  //   contents of rom_1 (hex, n*v repeats v):
  //   c 4a 30
endmodule

module IC_memory (
  input  in_1,
  input  in_2,
  input  in_3,
  input  in_4,
  input  in_5,
  input  in_6,
  input  in_7,
  input  in_8,
  input  in_9,
  input  in_10,
  input  in_11,
  input  in_12,
  input  in_13,
  input  in_14,
  input  in_15,
  input  in_16,
  input  in_17,
  input  in_18,
  input  in_19,
  input  in_20,
  input  in_21,
  input  in_22,
  input  in_23,
  input  in_24,
  input  in_25,
  input  in_26,
  input  in_27,
  input  in_28,
  input  in_29,
  input  in_30,
  input  in_31,
  input  in_32,
  input  in_33,
  input  in_34,
  input  in_35,
  input  in_36,
  input  in_37,
  input  in_38,
  input  in_39,
  input  in_40,
  input  in_41,
  input  in_42,
  input  in_43,
  input  in_44,
  input  in_45,
  input  in_46,
  input  in_47,
  input  in_48,
  input  in_49,
  input  in_50,
  input  in_51,
  input  in_52,
  input  in_53,
  input  in_54,
  input  in_55,
  input  in_56,
  input  in_57,
  input  in_58,
  input  in_59,
  input  in_60,
  input  in_61,
  input  in_62,
  input  in_63,
  input  in_64,
  input  in_65,
  input  in_66,
  input  in_67,
  input  in_68,
  input  in_69,
  input  in_70,
  input  in_71,
  input  in_72,
  input  in_73,
  input  in_74,
  input  in_75,
  input  in_76,
  input  in_77
);

  _74189 u_74189_1 (
    .S3(in_11), .D3(in_7), .S4(in_10), .D4(in_6), .A3(in_5), .A2(in_4), .A1(in_3), .S2(in_12), .D2(in_8),
    .S1(in_13), .D1(in_9), .WE(in_1), .A0(in_2));  // open: Vcc, GND, ME
  _74189 u_74189_2 (
    .S3(in_4), .D3(in_15), .S4(in_18), .D4(in_14), .A3(in_5), .A2(in_4), .A1(in_3), .S2(in_20), .D2(in_16),
    .S1(in_21), .D1(in_17), .ME(in_1), .A0(in_2));  // open: Vcc, GND, WE
  _74189 u_74189_3 (
    .S3(in_27), .D3(in_23), .S4(in_26), .D4(in_22), .A3(in_5), .A2(in_4), .A1(in_3), .S2(in_28), .D2(in_24),
    .S1(in_29), .D1(in_25), .ME(in_1), .A0(in_2));  // open: Vcc, GND, WE
  _74189 u_74189_4 (
    .S3(in_35), .D3(in_31), .S4(in_34), .D4(in_30), .A3(in_5), .A2(in_4), .A1(in_3), .S2(in_36), .D2(in_32),
    .S1(in_37), .D1(in_33), .ME(in_1), .A0(in_2));  // open: Vcc, GND, WE
  _74189 u_74189_5 (
    .S3(in_3), .D3(in_39), .S4(in_42), .D4(in_38), .A3(in_5), .A2(in_4), .A1(in_3), .S2(in_44), .D2(in_40),
    .S1(in_45), .D1(in_41), .ME(in_1), .A0(in_2));  // open: Vcc, GND, WE
  _74189 u_74189_6 (
    .S3(in_51), .D3(in_47), .S4(in_50), .D4(in_46), .A3(in_5), .A2(in_4), .A1(in_3), .S2(in_52), .D2(in_48),
    .S1(in_53), .D1(in_49), .ME(in_1), .A0(in_2));  // open: Vcc, GND, WE
  _74189 u_74189_7 (
    .S3(in_59), .D3(in_55), .S4(in_58), .D4(in_54), .A3(in_5), .A2(in_4), .A1(in_3), .S2(in_60), .D2(in_56),
    .S1(in_61), .D1(in_57), .ME(in_1), .A0(in_2));  // open: Vcc, GND, WE
  _74189 u_74189_8 (
    .S3(in_67), .D3(in_63), .S4(in_66), .D4(in_62), .A3(in_5), .A2(in_4), .A1(in_3), .S2(in_68), .D2(in_64),
    .S1(in_69), .D1(in_65), .ME(in_1), .A0(in_2));  // open: Vcc, GND, WE
  _74189 u_74189_9 (
    .S3(in_75), .D3(in_71), .S4(in_74), .D4(in_70), .A3(in_5), .A2(in_4), .A1(in_3), .S2(in_76), .D2(in_72),
    .S1(in_77), .D1(in_73), .ME(in_1), .A0(in_2));  // open: Vcc, GND, WE

  assign in_19 = in_4;
  assign in_43 = in_3;
endmodule

module IC_microcomputer (
);

  IC_memory ic_memory_1 ();  // open: in_10, in_11, in_12, in_13, in_18, in_19, in_20, in_21, in_26, in_27, in_28, in_29, in_34, in_35, in_36, in_37, in_42, in_43, in_44, in_45, in_50, in_51, in_52, in_53, in_58, in_59, in_60, in_61, in_66, in_67, in_68, in_69, in_74, in_75, in_76, in_77, in_2, in_3, in_4, in_5, in_1, in_6, in_7, in_8, in_9, in_14, in_15, in_16, in_17, in_22, in_23, in_24, in_25, in_30, in_31, in_32, in_33, in_38, in_39, in_40, in_41, in_46, in_47, in_48, in_49, in_54, in_55, in_56, in_57, in_62, in_63, in_64, in_65, in_70, in_71, in_72, in_73
endmodule

module _4_bit_microcomputer (
  input  in_1,
  input  in_2,
  output [3:0] out_3
);

  wire clock_1_out, n4b_alu_1_out_5, n4b_alu_1_out_6, n4b_alu_1_out_7, R_out;
  wire [3:0] counter_1_q, multiplexer_1_out, ram_1_data, register_1_q, register_2_q, test_1_out_9;
  wire [27:0] rom_1_data;

  Counter #(.width(4), .max('hf)) counter_1 (
    .load(in_1), .D(test_1_out_9), .count(in_2), .Q(counter_1_q), .clk(clock_1_out));  // open: carry, clr
  Clock clock_1 (.out(clock_1_out));
  Button R (.out(R_out));
  Multiplexer #(.width(4)) multiplexer_1 (
    .in0(out_3), .in1(rom_1_data[15:12]), .out(multiplexer_1_out), .sel(rom_1_data[11]));  // open: en
  ROM #(.addrWidth(4), .dataWidth(28)) rom_1 (.addr(counter_1_q), .data(rom_1_data));  // open: sel
  Test test_1 (
    .out_9(test_1_out_9), .IF_TRUE(rom_1_data[3:0]), .IF_NOT(rom_1_data[7:4]), .in_3(rom_1_data[8]),
    .in_4(rom_1_data[9]), .in_5(rom_1_data[10]), .in_6(n4b_alu_1_out_5), .in_7(n4b_alu_1_out_6),
    .in_8(n4b_alu_1_out_7));
  RAM #(.addrWidth(4), .dataWidth(4), .bus("separate")) ram_1 (
    .addr(rom_1_data[27:24]), .din(multiplexer_1_out), .data(ram_1_data), .str(rom_1_data[23]),
    .clk(rom_1_data[22]), .ld(rom_1_data[21]), .clr(R_out));  // open: sel
  Register #(.width(4), .trigger("high")) register_1 (
    .D(ram_1_data), .Q(register_1_q), .clk(rom_1_data[20]));  // open: en, clr
  Register #(.width(4), .trigger("high")) register_2 (
    .D(ram_1_data), .Q(register_2_q), .clk(rom_1_data[19]));  // open: en, clr
  _4b_ALU u_4b_alu_1 (
    .A_input(register_1_q), .B_input(register_2_q), .in_1(rom_1_data[18:16]), .Output(out_3),
    .out_5(n4b_alu_1_out_5), .out_6(n4b_alu_1_out_6), .out_7(n4b_alu_1_out_7));

  // Notes on the sheet:
  //   Count By Blank:
  //   00001100  C
  //   01001010  4a
  //   00110000  30
  //   contents of rom_1 (hex, n*v repeats v):
  //   c101810 7100020 6900030 10044b c100050 7000060 6800070 80 c000090 10 70000a0 68000b0 b0
endmodule

module _4b_ALU (
  input  [2:0] in_1,
  input  [3:0] A_input,
  input  [3:0] B_input,
  output [3:0] Output,
  output out_5,
  output out_6,
  output out_7
);

  wire [3:0] adder_1_out, and_1_out, demultiplexer_1_out0, demultiplexer_1_out1, demultiplexer_1_out2,
       demultiplexer_1_out3, demultiplexer_1_out4, demultiplexer_1_out5, demultiplexer_2_out0,
       demultiplexer_2_out1, demultiplexer_2_out2, demultiplexer_2_out3, demultiplexer_2_out4,
       demultiplexer_2_out5, divider_1_out, multiplier_1_out, or_1_out, subtractor_1_out;

  Demultiplexer #(.select(3), .width(4)) demultiplexer_1 (
    .out0(demultiplexer_1_out0), .out1(demultiplexer_1_out1), .out2(demultiplexer_1_out2),
    .out3(demultiplexer_1_out3), .out4(demultiplexer_1_out4), .out5(demultiplexer_1_out5), .in(A_input),
    .sel(in_1));  // open: out6, out7, en
  Demultiplexer #(.select(3), .width(4)) demultiplexer_2 (
    .out0(demultiplexer_2_out0), .out1(demultiplexer_2_out1), .out2(demultiplexer_2_out2),
    .out3(demultiplexer_2_out3), .out4(demultiplexer_2_out4), .out5(demultiplexer_2_out5), .in(B_input),
    .sel(in_1));  // open: out6, out7, en
  Adder #(.width(4)) adder_1 (
    .a(demultiplexer_1_out0), .b(demultiplexer_2_out0), .out(adder_1_out));  // open: cin, cout
  Subtractor #(.width(4)) subtractor_1 (
    .a(demultiplexer_1_out1), .b(demultiplexer_2_out1), .out(subtractor_1_out));  // open: bin, bout
  Multiplier #(.width(4)) multiplier_1 (
    .a(demultiplexer_1_out2), .b(demultiplexer_2_out2), .out(multiplier_1_out));  // open: cin, cout
  Divider #(.width(4)) divider_1 (
    .a(demultiplexer_1_out3), .b(demultiplexer_2_out3), .out(divider_1_out));  // open: upper, rem
  assign and_1_out = demultiplexer_1_out4 & demultiplexer_2_out4;  // AND_Gate and_1, 4 bits wide
  assign or_1_out = demultiplexer_1_out5 | demultiplexer_2_out5;  // OR_Gate or_1, 4 bits wide
  Comparator #(.width(4)) comparator_1 (.a(A_input), .b(B_input), .gt(out_5), .eq(out_6), .lt(out_7));
  Multiplexer #(.select(3), .width(4)) multiplexer_1 (
    .in0(adder_1_out), .in1(subtractor_1_out), .in2(multiplier_1_out), .in3(divider_1_out), .in4(and_1_out),
    .in5(or_1_out), .out(Output), .sel(in_1));  // open: in6, in7, en
endmodule
