// Logisim project 16 bit brainfuck.circ as structural Verilog: 1 circuit, main circuit bf16
module bf16 (
  input  _1_RAM
);

  wire _2_2_out, _2_out, and_2_out, and_out, b_2_out, b_out, clock_1_out, comparator_1_eq, d_ff_1_q,
       or_1_out, or_2_out, or_3_out, str_out;
  wire [6:0] keyboard_1_data;
  wire [7:0] adder_3_out, counter_2_q, multiplexer_5_out, multiplexer_6_out, ram_1_data, rom_2_data;
  wire [15:0] adder_1_out, adder_2_out, multiplexer_1_out, multiplexer_2_out, multiplexer_3_out,
       multiplexer_4_out, register_1_q, register_2_q, rom_1_data;

  Clock clock_1 (.out(clock_1_out));
  Multiplexer #(.width(16), .disabled(0), .enable("false")) multiplexer_1 (
    .in0(adder_1_out), .in1(rom_1_data), .out(multiplexer_1_out), .sel(d_ff_1_q));
  Multiplexer #(.width(16), .disabled(0), .enable("false")) multiplexer_2 (
    .in0(16'h1), .in1(16'h2), .out(multiplexer_2_out), .sel(or_2_out));
  Counter #(.width(32), .max('hffffffff), .ongoal("stay")) counter_1 (
    .count(or_3_out), .clk(clock_1_out));  // open: load, D, Q, carry, clr
  Register #(.width(16)) register_1 (
    .D(adder_2_out), .en(multiplexer_3_out[1]), .Q(register_1_q), .clk(clock_1_out));  // open: clr
  Register #(.width(16)) register_2 (
    .D(multiplexer_1_out), .en(or_3_out), .Q(register_2_q), .clk(clock_1_out));  // open: clr
  Adder #(.width(16)) adder_1 (.a(register_2_q), .b(multiplexer_2_out), .out(adder_1_out));  // open: cin, cout
  Adder #(.width(16)) adder_2 (.a(multiplexer_4_out), .b(register_1_q), .out(adder_2_out));  // open: cin, cout
  D_Flip_Flop d_ff_1 (.clk(clock_1_out), .D(or_1_out), .Q(d_ff_1_q));  // open: Qn, preset, en, reset
  ROM #(.addrWidth(16), .dataWidth(16)) rom_1 (.addr(register_2_q), .data(rom_1_data));  // open: sel
  or or_1 (or_1_out, b_out, b_2_out);
  or or_2 (or_2_out, _2_out, _2_2_out);
  RAM #(.addrWidth(16), .bus("separate")) ram_1 (
    .addr(register_1_q), .din(multiplexer_5_out), .data(ram_1_data), .str(str_out), .clk(clock_1_out));  // open: sel, ld, clr
  Multiplexer #(.width(16), .disabled(0), .enable("false")) multiplexer_3 (
    .in0(rom_1_data), .in1(16'h1), .out(multiplexer_3_out), .sel(d_ff_1_q));
  and b (b_out, ~multiplexer_3_out[0], multiplexer_3_out[4], comparator_1_eq);  // AND_Gate
  and b_2 (b_2_out, multiplexer_3_out[0], multiplexer_3_out[4], ~comparator_1_eq);  // AND_Gate
  and _2 (_2_out, ~multiplexer_3_out[0], multiplexer_3_out[4], ~comparator_1_eq);  // AND_Gate
  and _2_2 (_2_2_out, multiplexer_3_out[0], multiplexer_3_out[4], comparator_1_eq);
  Comparator comparator_1 (.a({8{1'b0}}), .b(ram_1_data), .eq(comparator_1_eq));  // open: gt, lt
  or or_3 (or_3_out, multiplexer_3_out[0], multiplexer_3_out[1], multiplexer_3_out[2], multiplexer_3_out[3], multiplexer_3_out[4], multiplexer_3_out[5], multiplexer_3_out[6], multiplexer_3_out[7]);
  Multiplexer #(.width(16), .disabled(0)) multiplexer_4 (
    .in0(16'h1), .in1({16{1'b1}}), .out(multiplexer_4_out), .sel(multiplexer_3_out[0]),
    .en(multiplexer_3_out[1]));
  Multiplexer #(.width(8), .disabled(0), .enable("false")) multiplexer_5 (
    .in0(adder_3_out), .in1(multiplexer_6_out), .out(multiplexer_5_out), .sel(multiplexer_3_out[3]));
  and \and  (and_out, multiplexer_3_out[3], ~multiplexer_3_out[0]);  // AND_Gate
  Adder adder_3 (
    .a({{7{multiplexer_3_out[0]}}, multiplexer_3_out[2]}), .b(ram_1_data), .out(adder_3_out));  // open: cin, cout
  or str (str_out, multiplexer_3_out[2], and_2_out);
  and and_2 (and_2_out, multiplexer_3_out[3], multiplexer_3_out[0]);
  Multiplexer #(.width(8), .disabled(0), .enable("false")) multiplexer_6 (
    .in0({1'b0, keyboard_1_data}), .in1(rom_2_data), .out(multiplexer_6_out), .sel(_1_RAM));
  Counter counter_2 (.count(and_2_out), .Q(counter_2_q), .clk(clock_1_out));  // open: load, D, carry, clr
  Keyboard keyboard_1 (.clk(clock_1_out), .re(and_2_out), .data(keyboard_1_data));  // open: clr, avail
  TTY #(.cols(24)) tty_1 (.data(ram_1_data[6:0]), .clk(clock_1_out), .we(and_out));  // open: clr
  ROM rom_2 (.addr(counter_2_q), .data(rom_2_data));  // open: sel

  // Notes on the sheet:
  //   IP
  //   #Instr
  //   DP
  //   Instructions (ROM)
  //   Data (RAM)
  //   </>
  //   +/-
  //   bf16 cpu by briandef
  //   https://github.com/briandef/bf16
  //   stdin: 0-keyboard
endmodule
