// Logisim project nandcircuits.circ as structural Verilog
module xand_from_nands (
  input  in_1,
  input  in_2,
  output out_3
);

  wire nand_1_out, nand_2_out, nand_3_out;

  nand nand_1 (nand_1_out, in_1, in_2);
  nand nand_2 (nand_2_out, in_1, nand_1_out);
  nand nand_3 (nand_3_out, nand_1_out, in_2);
  nand nand_4 (out_3, nand_2_out, nand_3_out);
endmodule

module nand_circuit_to_replace_and_and_or (
  input  a,
  input  b,
  input  c,
  input  d,
  output \output 
);

  wire nand_1_out, nand_2_out;

  nand nand_1 (nand_1_out, c, d);
  nand nand_2 (nand_2_out, a, b);
  nand nand_3 (\output , nand_1_out, nand_2_out);
endmodule

// Adder
module nand_adder (
  input  clock,
  input  a0,
  input  b0,
  input  a1,
  input  b1,
  input  a2,
  input  b2,
  input  a3,
  input  b3,
  output q0,
  output q1,
  output q3,
  output q4,
  output q5
);

  wire nand_1_out, nand_2_out, nand_3_out, nand_4_out, nand_5_out, nand_6_out, nand_7_out, nand_8_out,
       nand_9_out, nand_10_out, nand_11_out, nand_12_out, nand_13_out, nand_14_out, nand_15_out, nand_16_out,
       nand_17_out, nand_18_out, nand_19_out, nand_20_out, nand_21_out, nand_22_out, nand_23_out,
       nand_24_out, nand_25_out, nand_26_out, nand_27_out, nand_28_out, nand_29_out, nand_30_out,
       nand_31_out, nand_32_out, nand_33_out, nand_34_out, nand_35_out, nand_36_out, nand_38_out,
       nand_40_out, nand_42_out, xor_1_out, xor_2_out, xor_3_out, xor_4_out;

  xor xor_1 (xor_1_out, b0, clock);
  xor xor_2 (xor_2_out, b1, clock);
  xor xor_3 (xor_3_out, b2, clock);
  xor xor_4 (xor_4_out, b3, clock);
  nand nand_1 (nand_1_out, a0, xor_1_out);
  nand nand_2 (nand_2_out, a1, xor_2_out);
  nand nand_3 (nand_3_out, a2, xor_3_out);
  nand nand_4 (nand_4_out, a3, xor_4_out);
  nand nand_5 (nand_5_out, a0, nand_1_out);
  nand nand_6 (nand_6_out, nand_1_out, xor_1_out);
  nand nand_7 (nand_7_out, a1, nand_2_out);
  nand nand_8 (nand_8_out, nand_2_out, xor_2_out);
  nand nand_9 (nand_9_out, a2, nand_3_out);
  nand nand_10 (nand_10_out, nand_3_out, xor_3_out);
  nand nand_11 (nand_11_out, a3, nand_4_out);
  nand nand_12 (nand_12_out, nand_4_out, xor_4_out);
  nand nand_13 (nand_13_out, nand_5_out, nand_6_out);
  nand nand_14 (nand_14_out, nand_7_out, nand_8_out);
  nand nand_15 (nand_15_out, nand_9_out, nand_10_out);
  nand nand_16 (nand_16_out, nand_11_out, nand_12_out);
  nand nand_17 (nand_17_out, nand_13_out, nand_18_out);
  nand nand_18 (nand_18_out, nand_13_out, clock);
  nand nand_19 (nand_19_out, nand_18_out, clock);
  nand nand_20 (nand_20_out, nand_14_out, nand_21_out);
  nand nand_21 (nand_21_out, nand_14_out, nand_38_out);
  nand nand_22 (nand_22_out, nand_21_out, nand_38_out);
  nand nand_23 (nand_23_out, nand_15_out, nand_24_out);
  nand nand_24 (nand_24_out, nand_15_out, nand_40_out);
  nand nand_25 (nand_25_out, nand_24_out, nand_40_out);
  nand nand_26 (nand_26_out, nand_16_out, nand_27_out);
  nand nand_27 (nand_27_out, nand_16_out, nand_42_out);
  nand nand_28 (nand_28_out, nand_27_out, nand_42_out);
  nand nand_29 (nand_29_out, xor_1_out, a0);
  nand nand_30 (nand_30_out, nand_13_out, clock);
  nand nand_31 (nand_31_out, xor_2_out, a1);
  nand nand_32 (nand_32_out, nand_14_out, nand_38_out);
  nand nand_33 (nand_33_out, xor_3_out, a2);
  nand nand_34 (nand_34_out, nand_15_out, nand_40_out);
  nand nand_35 (nand_35_out, xor_4_out, a3);
  nand nand_36 (nand_36_out, nand_16_out, nand_42_out);
  nand nand_37 (q0, nand_17_out, nand_19_out);
  nand nand_38 (nand_38_out, nand_29_out, nand_30_out);
  nand nand_39 (q1, nand_20_out, nand_22_out);
  nand nand_40 (nand_40_out, nand_31_out, nand_32_out);
  nand nand_41 (q3, nand_23_out, nand_25_out);
  nand nand_42 (nand_42_out, nand_33_out, nand_34_out);
  nand nand_43 (q4, nand_26_out, nand_28_out);
  nand nand_44 (q5, nand_35_out, nand_36_out);
endmodule

module Register (
  input  Clock,
  input  D0,
  input  D1,
  input  D2,
  input  D3,
  output Q0,
  output Q1,
  output Q2,
  output Q3
);

  D_Flip_Flop d_ff_1 (.clk(Clock), .D(D0), .Q(Q0));  // open: Qn, preset, en, reset
  D_Flip_Flop d_ff_2 (.clk(Clock), .D(D1), .Q(Q1));  // open: Qn, preset, en, reset
  D_Flip_Flop d_ff_3 (.clk(Clock), .D(D2), .Q(Q2));  // open: Qn, preset, en, reset
  D_Flip_Flop d_ff_4 (.clk(Clock), .D(D3), .Q(Q3));  // open: Qn, preset, en, reset
endmodule

module RAM (
  input  clock,
  input  a0,
  input  a1,
  input  d0,
  input  d1,
  input  d2,
  input  d3,
  output out_8,
  output out_9,
  output out_10,
  output out_11
);

  wire and_5_out, and_6_out, and_7_out, and_8_out, not_1_out, not_2_out;
  wire [3:0] and_9_out, and_10_out, and_11_out, and_12_out, d_ff_4_q, d_ff_8_q, d_ff_12_q, d_ff_16_q;
  wire [3:3] and_1_out, and_2_out, and_3_out, and_4_out;

  not not_1 (not_1_out, a0);
  not not_2 (not_2_out, a1);
  and and_1 (and_1_out[3], not_1_out, not_2_out);
  and and_2 (and_2_out[3], not_2_out, a0);
  and and_3 (and_3_out[3], a1, not_1_out);
  and and_4 (and_4_out[3], a1, a0);
  and and_5 (and_5_out, clock, and_1_out[3]);
  D_Flip_Flop d_ff_1 (.clk(and_5_out), .D(d3), .Q(d_ff_4_q[3]));  // open: Qn, preset, en, reset
  D_Flip_Flop d_ff_2 (.clk(and_5_out), .D(d2), .Q(d_ff_4_q[2]));  // open: Qn, preset, en, reset
  D_Flip_Flop d_ff_3 (.clk(and_5_out), .D(d1), .Q(d_ff_4_q[1]));  // open: Qn, preset, en, reset
  D_Flip_Flop d_ff_4 (.clk(and_5_out), .D(d0), .Q(d_ff_4_q[0]));  // open: Qn, preset, en, reset
  and and_6 (and_6_out, clock, and_2_out[3]);
  D_Flip_Flop d_ff_5 (.clk(and_6_out), .D(d3), .Q(d_ff_8_q[3]));  // open: Qn, preset, en, reset
  D_Flip_Flop d_ff_6 (.clk(and_6_out), .D(d2), .Q(d_ff_8_q[2]));  // open: Qn, preset, en, reset
  D_Flip_Flop d_ff_7 (.clk(and_6_out), .D(d1), .Q(d_ff_8_q[1]));  // open: Qn, preset, en, reset
  D_Flip_Flop d_ff_8 (.clk(and_6_out), .D(d0), .Q(d_ff_8_q[0]));  // open: Qn, preset, en, reset
  and and_7 (and_7_out, clock, and_3_out[3]);
  D_Flip_Flop d_ff_9 (.clk(and_7_out), .D(d3), .Q(d_ff_12_q[3]));  // open: Qn, preset, en, reset
  D_Flip_Flop d_ff_10 (.clk(and_7_out), .D(d2), .Q(d_ff_12_q[2]));  // open: Qn, preset, en, reset
  D_Flip_Flop d_ff_11 (.clk(and_7_out), .D(d1), .Q(d_ff_12_q[1]));  // open: Qn, preset, en, reset
  D_Flip_Flop d_ff_12 (.clk(and_7_out), .D(d0), .Q(d_ff_12_q[0]));  // open: Qn, preset, en, reset
  and and_8 (and_8_out, clock, and_4_out[3]);
  D_Flip_Flop d_ff_13 (.clk(and_8_out), .D(d3), .Q(d_ff_16_q[3]));  // open: Qn, preset, en, reset
  D_Flip_Flop d_ff_14 (.clk(and_8_out), .D(d2), .Q(d_ff_16_q[2]));  // open: Qn, preset, en, reset
  D_Flip_Flop d_ff_15 (.clk(and_8_out), .D(d1), .Q(d_ff_16_q[1]));  // open: Qn, preset, en, reset
  D_Flip_Flop d_ff_16 (.clk(and_8_out), .D(d0), .Q(d_ff_16_q[0]));  // open: Qn, preset, en, reset
  assign and_9_out = d_ff_4_q & {4{and_1_out[3]}};  // AND_Gate and_9, 4 bits wide
  assign and_10_out = d_ff_8_q & {4{and_2_out[3]}};  // AND_Gate and_10, 4 bits wide
  assign and_11_out = d_ff_12_q & {4{and_3_out[3]}};  // AND_Gate and_11, 4 bits wide
  assign and_12_out = d_ff_16_q & {4{and_4_out[3]}};  // AND_Gate and_12, 4 bits wide
  assign {out_11, out_10, out_9, out_8} = and_9_out | and_10_out | and_11_out | and_12_out;  // OR_Gate or_1, 4 bits wide

  // Notes on the sheet:
  //   Ands can be replaced by mosefets
endmodule

module multiplexor (
  input  in_1,
  input  in_2,
  input  in_3,
  input  in_4,
  input  in_5,
  input  in_6,
  input  in_7,
  input  in_8,
  input  in_9,
  output out_10,
  output out_11,
  output out_12,
  output out_13
);

  wire [3:0] and_1_out, and_2_out, not_1_out;

  assign not_1_out = ~{4{in_9}};  // NOT_Gate not_1, 4 bits wide
  assign and_1_out = not_1_out & {in_1, in_2, in_3, in_4};  // AND_Gate and_1, 4 bits wide
  assign {out_10, out_11, out_12, out_13} = and_1_out | and_2_out;  // OR_Gate or_1, 4 bits wide
  assign and_2_out = {4{in_9}} & {in_5, in_6, in_7, in_8};  // AND_Gate and_2, 4 bits wide

  // Notes on the sheet:
  //   Can be done by mosfets
endmodule

module microcomputer (
  input  [10:0] in_1,
  input  in_2,
  input  in_3
);

  wire A_q0, A_q1, A_q2, A_q3, B_q0, B_q1, B_q2, B_q3, clock_1_out, clock_2_out, multiplexor_1_out_10,
       multiplexor_1_out_11, multiplexor_1_out_12, multiplexor_1_out_13, nand_adder_1_p11, nand_adder_1_p12,
       nand_adder_1_p13, nand_adder_1_p14, ram_2_out_8, ram_2_out_9, ram_2_out_10, ram_2_out_11;
  wire [3:0] counter_1_q;
  wire [10:0] ram_1_data;

  Counter #(.width(4), .max('hf)) counter_1 (
    .load(in_2), .count(in_3), .Q(counter_1_q), .clk(clock_1_out));  // open: D, carry, clr
  Clock clock_1 (.out(clock_1_out));
  Clock clock_2 (.out(clock_2_out));
  RAM_part #(.addrWidth(4), .dataWidth(11), .bus("separate")) ram_1 (
    .addr(counter_1_q), .din(in_1), .data(ram_1_data), .clk(clock_2_out));  // open: str, sel, ld, clr
  multiplexor multiplexor_1 (
    .in_9(ram_1_data[10]), .in_1(ram_1_data[6]), .in_2(ram_1_data[7]), .in_3(ram_1_data[8]),
    .in_4(ram_1_data[9]), .in_5(nand_adder_1_p14), .in_6(nand_adder_1_p13), .in_7(nand_adder_1_p12),
    .in_8(nand_adder_1_p11), .out_10(multiplexor_1_out_10), .out_11(multiplexor_1_out_11),
    .out_12(multiplexor_1_out_12), .out_13(multiplexor_1_out_13));
  RAM ram_2 (
    .a0(ram_1_data[1]), .a1(ram_1_data[0]), .d0(multiplexor_1_out_13), .d1(multiplexor_1_out_12),
    .d2(multiplexor_1_out_11), .d3(multiplexor_1_out_10), .clock(ram_1_data[2]), .out_8(ram_2_out_8),
    .out_9(ram_2_out_9), .out_10(ram_2_out_10), .out_11(ram_2_out_11));
  Register A (
    .D0(ram_2_out_8), .D1(ram_2_out_9), .D2(ram_2_out_10), .D3(ram_2_out_11), .Clock(ram_1_data[4]),
    .Q0(A_q0), .Q1(A_q1), .Q2(A_q2), .Q3(A_q3));
  Register B (
    .D0(ram_2_out_8), .D1(ram_2_out_9), .D2(ram_2_out_10), .D3(ram_2_out_11), .Clock(ram_1_data[3]),
    .Q0(B_q0), .Q1(B_q1), .Q2(B_q2), .Q3(B_q3));
  // nand_adder nand_adder_1: pin names not known; wires that end beside it: A_q0, A_q1, A_q2, A_q3, B_q0, B_q1, B_q2, B_q3, B_q3, ram_1_data[5], nand_adder_1_p11, nand_adder_1_p12, nand_adder_1_p13, nand_adder_1_p14

  // Notes on the sheet:
  //   Can be done by MANY switches
endmodule

module comparator2 (
  input  a,
  input  b,
  input  a_2,
  input  b_2,
  input  a_3,
  input  b_3,
  input  a_4,
  input  b_4,
  output A_B,
  output A_B_2,
  output A_B_3
);

  wire and_1_out, and_2_out, and_3_out, and_4_out, and_5_out, and_6_out, and_7_out, and_8_out, and_9_out,
       and_10_out, and_11_out, and_12_out, and_13_out, and_14_out, nor_1_out, nor_2_out, nor_3_out,
       nor_4_out, not_1_out, not_2_out, not_3_out, not_4_out, not_5_out, not_6_out, not_7_out, not_8_out;

  not not_1 (not_1_out, a);
  and and_1 (and_1_out, not_1_out, b);
  and and_2 (and_2_out, a, not_2_out);
  not not_2 (not_2_out, b);
  not not_3 (not_3_out, a_2);
  and and_3 (and_3_out, not_3_out, b_2);
  and and_4 (and_4_out, a_2, not_4_out);
  not not_4 (not_4_out, b_2);
  not not_5 (not_5_out, a_3);
  and and_5 (and_5_out, not_5_out, b_3);
  and and_6 (and_6_out, a_3, not_6_out);
  not not_6 (not_6_out, b_3);
  not not_7 (not_7_out, a_4);
  and and_7 (and_7_out, not_7_out, b_4);
  and and_8 (and_8_out, a_4, not_8_out);
  not not_8 (not_8_out, b_4);
  nor nor_1 (nor_1_out, and_1_out, and_2_out);
  nor nor_2 (nor_2_out, and_3_out, and_4_out);
  nor nor_3 (nor_3_out, and_5_out, and_6_out);
  nor nor_4 (nor_4_out, and_7_out, and_8_out);
  and and_9 (and_9_out, and_3_out, nor_1_out);
  and and_10 (and_10_out, nor_1_out, and_4_out);
  and and_11 (and_11_out, nor_2_out, nor_1_out, and_5_out);
  and and_12 (and_12_out, nor_2_out, nor_1_out, and_6_out);
  and and_13 (and_13_out, nor_2_out, nor_1_out, nor_3_out, and_7_out);
  and and_14 (and_14_out, nor_2_out, nor_1_out, nor_3_out, and_8_out);
  or or_1 (A_B_3, and_1_out, and_9_out, and_11_out, and_13_out);
  or or_2 (A_B, and_2_out, and_10_out, and_12_out, and_14_out);
  nor nor_5 (A_B_2, A_B_3, A_B);
endmodule

module compatrator_test (
  input  in_1,
  input  in_2,
  input  in_3,
  input  in_4
);

  wire and_1_out, clock_1_out, counter_2_carry, not_1_out;
  wire [2:0] comparator2_1_a_b, comparator_1_gt, xnor_1_out;
  wire [3:0] counter_1_q, counter_2_q;

  Counter #(.width(4), .max('hf)) counter_1 (
    .load(in_1), .count(in_2), .Q(counter_1_q), .clk(counter_2_carry));  // open: D, carry, clr
  Counter #(.width(4), .max('hf)) counter_2 (
    .load(in_3), .count(in_4), .Q(counter_2_q), .carry(counter_2_carry), .clk(clock_1_out));  // open: D, clr
  Clock clock_1 (.out(clock_1_out));
  comparator2 comparator2_1 (
    .a(counter_1_q[0]), .b(counter_2_q[0]), .a_2(counter_1_q[1]), .b_2(counter_2_q[1]), .a_3(counter_1_q[2]),
    .b_3(counter_2_q[2]), .a_4(counter_1_q[3]), .b_4(counter_2_q[3]), .A_B(comparator2_1_a_b[0]),
    .A_B_2(comparator2_1_a_b[1]), .A_B_3(comparator2_1_a_b[2]));
  Comparator #(.width(4), .mode("unsigned")) comparator_1 (
    .a(counter_1_q), .b(counter_2_q), .gt(comparator_1_gt[0]), .eq(comparator_1_gt[1]),
    .lt(comparator_1_gt[2]));
  assign xnor_1_out = ~(comparator2_1_a_b ^ comparator_1_gt);  // XNOR_Gate xnor_1, 3 bits wide
  Counter counter_3 (.clk(not_1_out));  // open: load, D, count, Q, carry, clr
  not not_1 (not_1_out, and_1_out);
  and and_1 (and_1_out, xnor_1_out[0], xnor_1_out[1], xnor_1_out[2]);
endmodule
