// Logisim project new brainfuck.circ as structural Verilog: 6 circuits, main circuit main
module main (
);

  wire clock_1_out, comparator_1_eq, comparator_2_eq, counter_controller_1_count, counter_controller_1_load,
       counter_controller_2_count, counter_controller_2_load, counter_controller_3_count,
       counter_controller_3_load, decoder_1_out0, decoder_1_out1, decoder_1_out2, decoder_1_out3,
       decoder_2_out0, decoder_2_out1, decoder_2_out2, decoder_2_out3, decoder_2_out6, decoder_2_out7,
       logic_ram_1_count____0_2, logic_ram_1_instruction_minus, logic_ram_1_instruction_plus,
       logic_ram_1_loop_minus, logic_ram_1_loop_plus, n1_1_tape____0, not_1_out;
  wire [1:0] counter_2_q;
  wire [3:0] IR_q, multiplexer_1_out;
  wire [6:0] keyboard_1_data;
  wire [7:0] counter_3_q, multiplexer_2_out, n1_1_out_11, ram_1_data, register_1_q, rom_1_data;
  wire [15:0] counter_1_q, counter_4_q, counter_controller_1_out_4, counter_controller_3_out_4;

  Counter_Controller counter_controller_1 (
    .Add(logic_ram_1_instruction_plus), .Sub(logic_ram_1_instruction_minus),
    .Load(counter_controller_1_load), .out_4(counter_controller_1_out_4), .Count(counter_controller_1_count));
  Counter #(.width(16), .max('hffff)) counter_1 (
    .load(counter_controller_1_load), .D(counter_controller_1_out_4), .count(counter_controller_1_count),
    .Q(counter_1_q), .clk(decoder_1_out0));  // open: carry, clr
  Decoder #(.select(2)) decoder_1 (
    .out0(decoder_1_out0), .out1(decoder_1_out1), .out2(decoder_1_out2), .out3(decoder_1_out3),
    .sel(counter_2_q));  // open: en
  Counter #(.width(2), .max('h3)) counter_2 (.Q(counter_2_q), .clk(clock_1_out));  // open: load, D, count, carry, clr
  Clock clock_1 (.out(clock_1_out));
  Multiplexer #(.width(4), .enable("false")) multiplexer_1 (
    .in0(rom_1_data[3:0]), .in1(rom_1_data[7:4]), .out(multiplexer_1_out), .sel(counter_1_q[15]));
  ROM #(.addrWidth(15)) rom_1 (.addr(counter_1_q[14:0]), .data(rom_1_data));  // open: sel
  LOGIC_RAM logic_ram_1 (
    .count____0(comparator_1_eq), .Count____1(comparator_2_eq), .Instruction_0(IR_q[0]),
    .Instruction_1(IR_q[1]), .Instruction_2(IR_q[2]), .Searching_Command__0(multiplexer_1_out[0]),
    .Searching_Command__1(multiplexer_1_out[1]), .Searching_Command__2(multiplexer_1_out[2]),
    .Tape____0(n1_1_tape____0), .Instruction_plus(logic_ram_1_instruction_plus),
    .Instruction_minus(logic_ram_1_instruction_minus), .Count____0_2(logic_ram_1_count____0_2),
    .Loop_plus(logic_ram_1_loop_plus), .Loop_minus(logic_ram_1_loop_minus));  // open: out_10, out_11, out_12
  Counter_Controller counter_controller_2 (
    .Add(logic_ram_1_loop_plus), .Sub(logic_ram_1_loop_minus), .Load(counter_controller_2_load),
    .Count(counter_controller_2_count));  // open: out_4
  Counter counter_3 (
    .load(counter_controller_2_load), .count(counter_controller_2_count), .Q(counter_3_q),
    .clk(decoder_1_out3));  // open: D, carry, clr
  Register #(.width(4)) IR (
    .D(multiplexer_1_out), .en(logic_ram_1_count____0_2), .Q(IR_q), .clk(decoder_1_out1));  // open: clr
  Comparator comparator_1 (.a(counter_3_q), .b({8{1'b0}}), .eq(comparator_1_eq));  // open: gt, lt
  Comparator comparator_2 (.a(counter_3_q), .b({8{1'b1}}), .eq(comparator_2_eq));  // open: gt, lt
  Decoder #(.select(3)) decoder_2 (
    .out0(decoder_2_out0), .out1(decoder_2_out1), .out2(decoder_2_out2), .out3(decoder_2_out3),
    .out6(decoder_2_out6), .out7(decoder_2_out7), .sel(IR_q[2:0]));  // open: out4, out5, en
  LOGIC_RAM_2 logic_ram_2_1 ();  // open: count____0, Count____1, Instruction_0, Instruction_1, Instruction_2, Searching_Command__0, Searching_Command__1, Searching_Command__2, Tape____0, out_10, out_11, out_12, Instruction_plus, Instruction_minus, Count____0_2, Loop_plus, Loop_minus
  LOGIC_RAM_3 logic_ram_3_1 ();  // open: count____0, Count____1, Instruction_0, Instruction_1, Instruction_2, Searching_Command__0, Searching_Command__1, Searching_Command__2, Tape____0, out_10, out_11, out_12, Instruction_plus, Instruction_minus, Count____0_2, Loop_plus, Loop_minus
  Counter_Controller counter_controller_3 (
    .Add(decoder_2_out2), .Sub(decoder_2_out3), .Load(counter_controller_3_load),
    .out_4(counter_controller_3_out_4), .Count(counter_controller_3_count));
  Counter #(.width(16), .max('hffff)) counter_4 (
    .load(counter_controller_3_load), .D(counter_controller_3_out_4), .count(counter_controller_3_count),
    .Q(counter_4_q), .clk(decoder_1_out2));  // open: carry, clr
  Multiplexer #(.width(8)) multiplexer_2 (
    .in0(n1_1_out_11), .in1({1'b0, keyboard_1_data}), .out(multiplexer_2_out), .sel(decoder_2_out7));  // open: en
  TTY tty_1 (.data(register_1_q[6:0]), .clk(decoder_2_out6));  // open: we, clr
  not not_1 (not_1_out, decoder_1_out2);
  Keyboard #(.trigger("falling")) keyboard_1 (.clk(decoder_2_out7), .data(keyboard_1_data));  // open: re, clr, avail
  RAM #(.addrWidth(16), .bus("separate")) ram_1 (
    .addr(counter_4_q), .din(multiplexer_2_out), .data(ram_1_data), .str(not_1_out), .sel(1'b1),
    .clk(decoder_1_out2), .ld(decoder_1_out2));  // open: clr
  Register #(.trigger("falling")) register_1 (.D(ram_1_data), .Q(register_1_q), .clk(decoder_1_out2));  // open: en, clr
  _1 u_1_1 (
    .in_1(decoder_2_out0), .in_2(decoder_2_out1), .in_3(register_1_q[0]), .in_4(register_1_q[1]),
    .in_5(register_1_q[2]), .in_6(register_1_q[3]), .in_7(register_1_q[4]), .in_8(register_1_q[5]),
    .in_9(register_1_q[6]), .in_10(register_1_q[7]), .out_11(n1_1_out_11[0]), .out_12(n1_1_out_11[1]),
    .out_13(n1_1_out_11[2]), .out_14(n1_1_out_11[3]), .out_15(n1_1_out_11[4]), .out_16(n1_1_out_11[5]),
    .out_17(n1_1_out_11[6]), .out_18(n1_1_out_11[7]), .Tape____0(n1_1_tape____0));

  // Notes on the sheet:
  //   Breaking up clock signal into 2x and 1x
  //   32k x 8 ROM (64k x 4)
  //   contents of rom_1 (hex, n*v repeats v):
  //   4*2 0 0 2 0 2 0 0 2 0 2 2 0 0 3 3 4 1 1 4 0 4 0 0 0 4*3 1 1 5 0 0 4*2 1 1 5 0 4 4*3 5 2 4 2 4 4*2 5
  //   0 3 5 2 1 4*3 4 4*3 5 4*2 4 2 2 4 4*2 5 4*3 4 4 4*2 0 4*3 1 5 4*3 5 6*2 5 2 2 4 4*2 5 4*3 4 3 3 0 3
  //   0 3 5 3 3 4 6*2 4 4 4*3 0 4*2 1 5 4*2 5 8*3 4 4*3 5 2 2 1 4 3 3 0 2 2 1 5 0 3 3 4 1 4*2 4 1 4 0 4*2
  //   1 5 1 3 3 1 4 4*2 1 5 0 0 2 2 0 4 1 4*3 0 5 0 4*2 5 4*3 4 4*3 5 5 2 4 1 4 3 0 2 1 5 5 0 3 4 1 4*2 4
  //   1 4 0 4*2 1 5 1 3 3 3 1 4 4*2 1 5 0 0 2 2 2 0 4 1 4*3 0 5 0 4*2 5 4*3 4 4*3 5 5 3 3 5 2 2 2 0 4 4*2
  //   5 1 4 0 4*3 1 1 5 0 0 4 4*3 5 2 2 2 0 4 2 1 4 2 2 4 1 1 4 0 0 2 2 0 2 2 1 1 5 1 3 4 1 4 1 4 0 0 0
  //   4*3 1 5 0 4*2 1 5 5 0 0 2 0 4 1 4*3 0 5 0 0 2 2 0 2 2 5 3 3 1 4*3 4 2 4 3 1 3 3 3 5 0 3 5 2 1 2 2 2
  //   5 0 2 4 4*2 5 1 4 0 4*3 1 1 5 0 0 3 4 4 4*2 5 4*3 4 1 4 1 2 1 1 4 3 1 2 0 5 0 0 3 4 4 2 1 3 0 5 0 0
  //   4 4*3 5 0 2 2 0 2 2 1 5 0 0 4*3 1 5 2 1 4 0 4 3 0 4 4*3 5 2 5 2 2 2 4 1 5 2 1 4 3 0 2 1 5 5 0 3 4 2
  //   0 3 1 5 0 4*3 5 5 2 4 4*3 5 2 4 1 4 1 4 1 2 1 4 3 3 0 2 0 2 1 5 6*0 4 3 8*0 2 1 5 3 6 1 1 3 4 2 1 3
  //   1 5 5*2 1 1 4 3 5 3 3 4 3 3 6 3 5 2 4 1 5 2 2 1 2 2 0 0 4 4 4*2 5 0 4 1 4 1 4*2 0 8*2 1 4 1 4 0 0 0
  //   4*3 4 1 5 5 0 4*2 1 5 0 0 4 4*3 5 5 0 4*3 5 2 2 2 5 0 3 0 3 3 5 2 4 1 4 1 2 4 1 1 4 0 0 4*2 1 1 5 1
  //   2 4 1 4 1 4 0 0 0 4*3 1 5 0 4*2 1 5 5 0 0 3 0 4 1 4*3 0 5 0 0 4*2 5 4*3 4 2 4 4*3 5 0 3 5 2 1 2 2 5
  //   3 5 4*2 4 1 1 4 0 0 4*2 1 1 5 1 3 1 1 4 0 0 0 4*2 1 1 5 0 2 0 4 1 4*3 0 5 0 0 4*2 5 5*3 4 4*3 5 3 5
  //   2 4 2 0 3 3 0 0 3 5 3 5 2 4 0 2 4 1 1 4 0 0 4*2 1 1 5 1 2 1 1 4 0 0 0 4*2 1 1 5 0 3 0 4 1 4*3 0 5 0
  //   0 4*2 5 3 3 3 4 4*3 5 5 2 2 5 4*2 5
endmodule

// CC
module Counter_Controller (
  input  Add,
  input  Sub,
  output Load,
  output [15:0] out_4,
  output Count
);

  wire and_2_out, and_3_out, not_1_out, not_2_out, not_3_out;

  not not_1 (not_1_out, Add);
  not not_2 (not_2_out, Add);
  not not_3 (not_3_out, Sub);
  and and_1 (Load, not_1_out, Sub);
  and and_2 (and_2_out, not_2_out, Sub);
  and and_3 (and_3_out, Add, not_3_out);
  or or_1 (Count, and_2_out, and_3_out);

  assign out_4 = {16{1'b0}};
endmodule

module LOGIC_RAM (
  input  Instruction_0,
  input  Instruction_1,
  input  Instruction_2,
  input  Searching_Command__0,
  input  Searching_Command__1,
  input  Searching_Command__2,
  input  Tape____0,
  input  count____0,
  input  Count____1,
  output out_10,
  output out_11,
  output out_12,
  output Instruction_plus,
  output Instruction_minus,
  output Count____0_2,
  output Loop_plus,
  output Loop_minus
);

  wire and_2_out, and_3_out, and_5_out, and_6_out, and_7_out;

  // AND_Gate and has open pins: in0=Instruction_0, in1=Instruction_1, in2=Instruction_2, out=open
  and and_2 (and_2_out, Instruction_0, ~Instruction_1, Instruction_2);  // AND_Gate
  and and_3 (and_3_out, Count____1, and_2_out, and_6_out);
  and and_4 (Instruction_minus, and_2_out, ~and_3_out, Tape____0);  // AND_Gate
  not not_1 (Instruction_plus, Instruction_minus);
  and and_5 (and_5_out, and_2_out, Tape____0, and_6_out);
  and and_6 (and_6_out, ~Searching_Command__0, ~Searching_Command__1, Searching_Command__2);  // AND_Gate
  and and_7 (and_7_out, and_6_out, ~Tape____0);  // AND_Gate
  or or_1 (Loop_plus, and_5_out, and_7_out);
  and and_8 (Loop_minus, Searching_Command__0, ~Searching_Command__1, Searching_Command__2);  // AND_Gate

  assign Count____0_2 = count____0;
  assign out_10 = 1'b0;
  assign out_11 = 1'b0;
  assign out_12 = 1'b0;

  // Notes on the sheet:
  //   Instruction Command (From Reg)
  //   Searching Command
endmodule

module _1 (
  input  in_1,
  input  in_2,
  input  in_3,
  input  in_4,
  input  in_5,
  input  in_6,
  input  in_7,
  input  in_8,
  input  in_9,
  input  in_10,
  output out_11,
  output out_12,
  output out_13,
  output out_14,
  output out_15,
  output out_16,
  output out_17,
  output out_18,
  output Tape____0
);

  wire comparator_1_eq;
  wire [7:0] adder_1_out, subtractor_1_out;

  Subtractor subtractor_1 (
    .a({in_10, in_9, in_8, in_7, in_6, in_5, in_4, in_3}), .b(8'h1), .out(subtractor_1_out));  // open: bin, bout
  Adder adder_1 (
    .a(8'h1), .b({in_10, in_9, in_8, in_7, in_6, in_5, in_4, in_3}), .out(adder_1_out));  // open: cin, cout
  Multiplexer #(.select(2), .width(8)) multiplexer_1 (
    .in0({in_10, in_9, in_8, in_7, in_6, in_5, in_4, in_3}), .in1(adder_1_out), .in2(subtractor_1_out),
    .in3({in_10, in_9, in_8, in_7, in_6, in_5, in_4, in_3}),
    .out({out_18, out_17, out_16, out_15, out_14, out_13, out_12, out_11}), .sel({in_2, in_1}));  // open: en
  Comparator comparator_1 (
    .a({in_10, in_9, in_8, in_7, in_6, in_5, in_4, in_3}), .b({8{1'b0}}), .eq(comparator_1_eq));  // open: gt, lt
  not not_1 (Tape____0, comparator_1_eq);
endmodule

module LOGIC_RAM_2 (
  input  Instruction_0,
  input  Instruction_1,
  input  Instruction_2,
  input  Searching_Command__0,
  input  Searching_Command__1,
  input  Searching_Command__2,
  input  Tape____0,
  input  count____0,
  input  Count____1,
  output out_10,
  output out_11,
  output out_12,
  output Instruction_plus,
  output Instruction_minus,
  output Count____0_2,
  output Loop_plus,
  output Loop_minus
);

  wire and_2_out, and_4_out, and_5_out, and_6_out, and_7_out, and_8_out, and_9_out, and_out;

  and \and  (and_out, ~Instruction_0, ~Instruction_1, Instruction_2);  // AND_Gate
  not not_1 (Instruction_plus, Instruction_minus);
  and and_2 (and_2_out, Instruction_0, ~Instruction_1, Instruction_2);  // AND_Gate
  and and_3 (Instruction_minus, and_2_out, ~count____0);  // AND_Gate
  and and_4 (and_4_out, and_5_out, ~Tape____0);  // AND_Gate
  and and_5 (and_5_out, ~Searching_Command__0, ~Searching_Command__1, Searching_Command__2);  // AND_Gate
  and and_6 (and_6_out, and_5_out, and_2_out, Tape____0);
  or or_1 (Loop_plus, and_4_out, and_6_out);
  and and_7 (and_7_out, Searching_Command__0, ~Searching_Command__1, Searching_Command__2);  // AND_Gate
  and and_8 (and_8_out, and_7_out, and_out, ~Tape____0);  // AND_Gate
  and and_9 (and_9_out, and_7_out, Tape____0);
  or or_2 (Loop_minus, and_9_out, and_8_out);

  assign Count____0_2 = count____0;
  assign out_10 = 1'b0;
  assign out_11 = 1'b0;
  assign out_12 = 1'b0;

  // Notes on the sheet:
  //   Searching Command
endmodule

module LOGIC_RAM_3 (
  input  Instruction_0,
  input  Instruction_1,
  input  Instruction_2,
  input  Searching_Command__0,
  input  Searching_Command__1,
  input  Searching_Command__2,
  input  Tape____0,
  input  count____0,
  input  Count____1,
  output out_10,
  output out_11,
  output out_12,
  output Instruction_plus,
  output Instruction_minus,
  output Count____0_2,
  output Loop_plus,
  output Loop_minus
);

  // AND_Gate and has open pins: in0=Instruction_0, in1=Instruction_1, in2=Instruction_2, out=open
  not not_1 (Instruction_plus, Instruction_minus);
  // AND_Gate and_2 has open pins: in0=Instruction_0, in1=Instruction_1, in2=Instruction_2, out=open
  and and_3 (Instruction_minus, Count____1, ~Tape____0);  // AND_Gate
  and and_4 (Loop_plus, ~Searching_Command__0, ~Searching_Command__1, Searching_Command__2);  // AND_Gate
  and and_5 (Loop_minus, Searching_Command__0, ~Searching_Command__1, Searching_Command__2);  // AND_Gate

  assign out_10 = 1'b0;
  assign out_11 = 1'b0;
  assign out_12 = 1'b0;

  // Notes on the sheet:
  //   Searching Command
endmodule
